// Logisim project single_cycle-alu.circ as structural Verilog: 4 circuits, main circuit main
module main (
  input  PCSrc,
  input  RegWrite,
  input  [1:0] ALUSrc,
  input  [3:0] ALUOp,
  input  MemToRebg,
  input  MemWrite
);

  wire clock_1_out, clock_2_c0, clock_2_c1, clock_2_c3, undriven_2;
  wire [1:0] undriven_3;
  wire [7:0] alu_1_aluresult;
  wire [31:0] adder_1_out, bit_extender_1_out, bit_extender_2_out, Inst_q, Instruction_Memory_data,
       multiplexer_1_out, multiplexer_2_out, multiplexer_3_out, PC_q, ram_1_data, registerfile_1_d1,
       registerfile_1_d2, undriven;
  wire [31:8] alu_1_aluresult_2;

  Multiplexer #(.width(32), .enable("false")) multiplexer_1 (
    .in0(adder_1_out), .in1(undriven), .out(multiplexer_1_out), .sel(PCSrc));
  Clock clock_1 (.out(clock_1_out));
  Register #(.width(32), .Select("low")) PC (.D(multiplexer_1_out), .Q(PC_q), .clk(undriven_2));  // open: en, clr
  clock clock_2 (.c0(clock_2_c0), .c1(clock_2_c1), .c3(clock_2_c3), .clock(clock_1_out));  // open: c2, c4
  Adder #(.width(32)) adder_1 (.a(32'h4), .b(PC_q), .out(adder_1_out));  // open: cin, cout
  ROM #(.dataWidth(32), .Select("low")) Instruction_Memory (.addr(PC_q[9:2]), .data(Instruction_Memory_data));
  Register #(.width(32), .Select("low")) Inst (
    .D(Instruction_Memory_data), .Q(Inst_q), .clk(clock_2_c1));  // open: en, clr
  assign bit_extender_1_out = {{20{Inst_q[31]}}, Inst_q[31:20]};  // Bit_Extender bit_extender_1
  assign bit_extender_2_out = {{20{Inst_q[31]}}, {Inst_q[31:25], Inst_q[11:7]}};  // Bit_Extender bit_extender_2
  RegisterFile registerfile_1 (
    .Clock(clock_2_c1), .rs1(Inst_q[19:15]), .rs2(Inst_q[24:20]), .Write_register(Inst_q[11:7]),
    .Write_data(multiplexer_3_out), .RegWrite(RegWrite), .d1(registerfile_1_d1), .d2(registerfile_1_d2));
  Multiplexer #(.select(2), .width(32), .enable("false")) multiplexer_2 (
    .in0(registerfile_1_d2), .in1(bit_extender_1_out), .in2(bit_extender_2_out), .out(multiplexer_2_out),
    .sel(undriven_3));  // open: in3
  ALU alu_1 (
    .Operand_1(registerfile_1_d1), .Operand_2(multiplexer_2_out), .ALUOp(ALUOp),
    .ALUResult({alu_1_aluresult_2, alu_1_aluresult}));  // open: Clock, ShfAmt, Zero, Less_than_zero, Greater_than_zero
  RAM #(.dataWidth(32), .bus("separate"), .simpleMode("false"), .Select("low")) ram_1 (
    .addr(alu_1_aluresult), .din(registerfile_1_d2), .data(ram_1_data), .str(MemWrite), .clk(clock_2_c3));  // open: sel, ld, clr
  Multiplexer #(.width(32), .enable("false")) multiplexer_3 (
    .in0({alu_1_aluresult_2, alu_1_aluresult}), .in1(ram_1_data), .out(multiplexer_3_out), .sel(MemToRebg));

  // Notes on the sheet:
  //   R-type
  //   I-type
  //   B-type
endmodule

// RegFile
module RegisterFile (
  input  Clock,
  input  [4:0] rs1,
  input  [4:0] rs2,
  input  [4:0] Write_register,
  input  [31:0] Write_data,
  input  RegWrite,
  output [31:0] d1,
  output [31:0] d2
);


  // Notes on the sheet:
  //   Entradas
  //   Control
  //   Salidas
endmodule

module ALU (
  input  Clock,
  input  [31:0] Operand_1,
  input  [31:0] Operand_2,
  input  [4:0] ShfAmt,
  input  [3:0] ALUOp,
  output [31:0] ALUResult,
  output Zero,
  output Less_than_zero,
  output Greater_than_zero
);

  wire [31:0] shifter_1_out, shifter_2_out, shifter_3_out;

  Shifter #(.width(32)) shifter_1 (.in(Operand_1), .\dist (ShfAmt), .out(shifter_1_out));
  Shifter #(.width(32), .shift("lr")) shifter_2 (.in(Operand_1), .\dist (ShfAmt), .out(shifter_2_out));
  Shifter #(.width(32), .shift("ar")) shifter_3 (.in(Operand_1), .\dist (ShfAmt), .out(shifter_3_out));

  // Notes on the sheet:
  //   Entradas
  //   Control
  //   Salidas
endmodule

module clock (
  input  clock,
  output c0,
  output c1,
  output c2,
  output c3,
  output c4
);


  // Notes on the sheet:
  //   Entradas
  //   Salidas
endmodule
