// Logisim project lab03.circ as structural Verilog: 1 circuit, main circuit main
module main (
  input  [6:0] Opcode,
  output MemWrite,
  output Branch,
  output MemRead,
  output RegWrite,
  output MemToReg,
  output [2:0] ALU_Operation,
  output [1:0] Operand_A_Sel,
  output Operand_B_Sel,
  output [1:0] Extend_Sel,
  output [1:0] Next_PC_Sel
);

  wire and_1_out, and_2_out, and_3_out, and_5_out, and_6_out, and_7_out, and_8_out, comparator_1_eq,
       comparator_5_eq, comparator_6_eq, comparator_7_eq, not_1_out, not_2_out, not_3_out, not_4_out,
       not_5_out, not_6_out, not_7_out, not_8_out, not_9_out, not_10_out, not_11_out, not_12_out, not_13_out,
       not_14_out, not_15_out, not_16_out, not_17_out, not_18_out, not_19_out, not_20_out, not_21_out,
       not_22_out, not_23_out, not_24_out, not_25_out, not_26_out, not_27_out, not_28_out, not_29_out;

  Comparator #(.width(7), .mode("unsigned")) comparator_1 (
    .a(7'b0110011), .b(Opcode), .eq(comparator_1_eq));  // open: gt, lt
  Comparator #(.width(7), .mode("unsigned")) comparator_2 (.a(Opcode), .b(7'b0000011), .eq(MemRead));  // open: gt, lt
  Comparator #(.width(7), .mode("unsigned")) comparator_3 (
    .a(Opcode), .b(7'b0100011), .eq(Extend_Sel[1]));  // open: gt, lt
  Comparator #(.width(7), .mode("unsigned")) comparator_4 (.a(Opcode), .b(7'b1100011), .eq(Branch));  // open: gt, lt
  Comparator #(.width(7), .mode("unsigned")) comparator_5 (
    .a(Opcode), .b(7'b0010011), .eq(comparator_5_eq));  // open: gt, lt
  Comparator #(.width(7), .mode("unsigned")) comparator_6 (
    .a(Opcode), .b(7'b1100111), .eq(comparator_6_eq));  // open: gt, lt
  Comparator #(.width(7), .mode("unsigned")) comparator_7 (
    .a(Opcode), .b(7'b1101111), .eq(comparator_7_eq));  // open: gt, lt
  Comparator #(.width(7), .mode("unsigned")) comparator_8 (
    .a(Opcode), .b(7'b0110111), .eq(Extend_Sel[0]));  // open: gt, lt
  or or_1 (RegWrite, comparator_1_eq, MemRead, comparator_5_eq, Extend_Sel[0], comparator_7_eq, comparator_6_eq);
  not not_1 (not_1_out, Extend_Sel[0]);
  not not_2 (not_2_out, comparator_6_eq);
  not not_3 (not_3_out, Extend_Sel[0]);
  not not_4 (not_4_out, comparator_7_eq);
  not not_5 (not_5_out, comparator_6_eq);
  not not_6 (not_6_out, comparator_7_eq);
  not not_7 (not_7_out, comparator_6_eq);
  not not_8 (not_8_out, comparator_7_eq);
  or or_2 (Operand_B_Sel, Extend_Sel[0], comparator_5_eq, Extend_Sel[1], MemRead);
  and and_1 (and_1_out, not_1_out, not_2_out, comparator_7_eq);
  and and_2 (and_2_out, not_3_out, comparator_6_eq, not_4_out);
  and and_3 (and_3_out, Extend_Sel[0], not_5_out, not_6_out);
  and and_4 (Operand_A_Sel[0], Extend_Sel[0], not_7_out, not_8_out);
  not not_9 (not_9_out, Extend_Sel[1]);
  not not_10 (not_10_out, comparator_7_eq);
  and and_5 (and_5_out, not_9_out, not_10_out, comparator_6_eq);
  not not_11 (not_11_out, Extend_Sel[1]);
  and and_6 (and_6_out, not_11_out, comparator_7_eq, not_12_out);
  not not_12 (not_12_out, comparator_6_eq);
  not not_13 (not_13_out, Extend_Sel[1]);
  not not_14 (not_14_out, comparator_7_eq);
  and and_7 (and_7_out, not_13_out, not_14_out, comparator_6_eq);
  and and_8 (and_8_out, Extend_Sel[1], not_15_out, not_16_out);
  not not_15 (not_15_out, comparator_7_eq);
  not not_16 (not_16_out, comparator_6_eq);
  not not_17 (not_17_out, comparator_1_eq);
  not not_18 (not_18_out, Branch);
  not not_19 (not_19_out, comparator_5_eq);
  not not_20 (not_20_out, comparator_6_eq);
  not not_21 (not_21_out, comparator_7_eq);
  not not_22 (not_22_out, comparator_1_eq);
  not not_23 (not_23_out, MemRead);
  not not_24 (not_24_out, Extend_Sel[1]);
  not not_25 (not_25_out, comparator_5_eq);
  not not_26 (not_26_out, comparator_1_eq);
  not not_27 (not_27_out, MemRead);
  not not_28 (not_28_out, Branch);
  not not_29 (not_29_out, Extend_Sel[0]);
  or or_3 (Operand_A_Sel[1], and_1_out, and_2_out, and_3_out);
  or or_4 (Next_PC_Sel[1], and_5_out, and_6_out);
  or or_5 (Next_PC_Sel[0], and_7_out, and_8_out);
  and and_9 (ALU_Operation[2], not_17_out, not_18_out, not_19_out, not_20_out, not_21_out);
  and and_10 (ALU_Operation[1], not_22_out, not_23_out, not_24_out, not_25_out);
  and and_11 (ALU_Operation[0], not_26_out, not_27_out, not_28_out, not_29_out);

  assign MemToReg = MemRead;
  assign MemWrite = Extend_Sel[1];

  // Notes on the sheet:
  //   R-Format
  //   Load
  //   Store
  //   Branch
  //   I-Type
  //   JALR
  //   JAL
  //   LUI
  //   Notese que yo en mi ALU tengo un parseador del ALU Operation, lo que me permitirá trabajar con esta salida
endmodule
