// Logisim project multi_cycle-riscv.circ as structural Verilog: 8 circuits, main circuit main
module main (
  input  X
);

  wire and_1_out, Clock, comparator_1_lt, comparator_2_eq, controlunit_1_out_6, controlunit_1_out_8,
       controlunit_1_out_9, controlunit_1_out_10, controlunit_1_out_11, controlunit_1_out_12,
       controlunit_1_out_13, PCWrite;
  wire [1:0] controlunit_1_out_3, controlunit_1_out_7;
  wire [2:0] Cycle, Funct3;
  wire [3:0] controlunit_1_out_4;
  wire [4:0] instructionregister_1_out_4, instructionregister_1_out_8, SftAmt;
  wire [6:0] OpCode;
  wire [15:0] counter_1_q, counter_2_q;
  wire [31:0] A_q, alu_1_aluresultado, B_q, bit_extender_1_out, bit_extender_2_out, bit_extender_3_out,
       bit_extender_4_out, instructionregister_1_out_9, memory_1_out_7, memorydataregister_1_out_3,
       multiplexer_1_out, multiplexer_2_out, multiplexer_4_out, multiplexer_5_out, multiplexer_6_out, PC_q,
       registerfile_1_readdata1, registerfile_1_readdata2, shifter_1_out, shifter_2_out;

  Register #(.width(32), .Select("low")) PC (.D(multiplexer_6_out), .en(PCWrite), .Q(PC_q), .clk(Clock));  // open: clr
  Comparator #(.width(32)) comparator_1 (.a(PC_q), .b(32'h38), .lt(comparator_1_lt));  // open: gt, eq
  Clock clock_1 (.out(Clock));
  ControlUnit controlunit_1 (
    .in_1(Clock), .out_3(controlunit_1_out_3), .out_5(Cycle), .out_6(controlunit_1_out_6),
    .out_7(controlunit_1_out_7), .out_8(controlunit_1_out_8), .out_9(controlunit_1_out_9),
    .out_10(controlunit_1_out_10), .out_11(controlunit_1_out_11), .out_12(controlunit_1_out_12),
    .out_13(controlunit_1_out_13), .in_2(instructionregister_1_out_9), .out_4(controlunit_1_out_4));
  Memory memory_1 (
    .in_1(multiplexer_1_out), .out_7(memory_1_out_7), .in_2(B_q), .in_3(controlunit_1_out_10),
    .in_4(controlunit_1_out_11), .in_5(Clock), .in_6(controlunit_1_out_8));
  Multiplexer #(.width(32), .enable("false")) multiplexer_1 (
    .in0(PC_q), .in1(memorydataregister_1_out_3), .out(multiplexer_1_out), .sel(controlunit_1_out_8));
  Counter #(.width(16), .max('hffff)) counter_1 (
    .count(comparator_1_lt), .Q(counter_1_q), .clk(Clock));  // open: load, D, carry, clr, preset, down
  // Probe on counter_1_q
  Comparator #(.width(3)) comparator_2 (.a(Cycle), .b(3'b000), .eq(comparator_2_eq));  // open: gt, lt
  and and_1 (and_1_out, comparator_2_eq, comparator_1_lt);
  Counter #(.width(16), .max('hffff)) counter_2 (
    .count(and_1_out), .Q(counter_2_q), .clk(Clock));  // open: load, D, carry, clr, preset, down
  InstructionRegister instructionregister_1 (
    .in_1(memory_1_out_7), .in_2(Clock), .out_4(instructionregister_1_out_4), .out_6(SftAmt),
    .out_8(instructionregister_1_out_8), .in_3(controlunit_1_out_9), .out_9(instructionregister_1_out_9),
    .out_5(OpCode), .out_7(Funct3));
  MemoryDataRegister memorydataregister_1 (.in_1(memory_1_out_7), .out_3(memorydataregister_1_out_3), .in_2(Clock));
  // Probe on counter_2_q
  Multiplexer #(.width(32), .enable("false")) multiplexer_2 (
    .in0(memorydataregister_1_out_3), .in1(memorydataregister_1_out_3), .out(multiplexer_2_out),
    .sel(controlunit_1_out_13));
  RegisterFile registerfile_1 (
    .Clock(Clock), .ReadRegister1(instructionregister_1_out_4), .ReadRegister2(SftAmt),
    .WriteRegister(instructionregister_1_out_8), .WriteData(multiplexer_2_out),
    .RegisterWrite(controlunit_1_out_12), .ReadData1(registerfile_1_readdata1),
    .ReadData2(registerfile_1_readdata2));
  assign bit_extender_1_out = {{20{instructionregister_1_out_9[31]}}, instructionregister_1_out_9[31:20]};  // Bit_Extender bit_extender_1
  assign bit_extender_2_out = {{20{instructionregister_1_out_9[31]}}, {instructionregister_1_out_9[31:25], instructionregister_1_out_9[11:7]}};  // Bit_Extender bit_extender_2
  assign bit_extender_3_out = {{19{instructionregister_1_out_9[31]}}, {instructionregister_1_out_9[31], instructionregister_1_out_9[8], instructionregister_1_out_9[30:25], instructionregister_1_out_9[12:9], 1'b0}};  // Bit_Extender bit_extender_3
  assign bit_extender_4_out = {{11{instructionregister_1_out_9[31]}}, {instructionregister_1_out_9[31], instructionregister_1_out_9[19:12], instructionregister_1_out_9[20], instructionregister_1_out_9[30:21], 1'b0}};  // Bit_Extender bit_extender_4
  Shifter #(.width(32)) shifter_1 (.in(bit_extender_3_out), .\dist (5'b00001), .out(shifter_1_out));
  Shifter #(.width(32)) shifter_2 (.in(bit_extender_4_out), .\dist (5'b00001), .out(shifter_2_out));
  Register #(.width(32), .Select("low")) A (.D(registerfile_1_readdata1), .Q(A_q), .clk(Clock));  // open: en, clr
  Register #(.width(32), .Select("low")) B (.D(registerfile_1_readdata2), .Q(B_q), .clk(Clock));  // open: en, clr
  Multiplexer #(.select(2), .width(32), .enable("false")) multiplexer_3 (
    .in0(bit_extender_1_out), .in1(bit_extender_2_out), .in2(shifter_1_out), .in3(shifter_2_out),
    .sel(controlunit_1_out_3));  // open: out
  Multiplexer #(.width(32), .enable("false")) multiplexer_4 (
    .in0(PC_q), .in1(A_q), .out(multiplexer_4_out), .sel(controlunit_1_out_6));
  Multiplexer #(.select(2), .width(32), .enable("false")) multiplexer_5 (
    .in0(B_q), .in1(32'h4), .out(multiplexer_5_out), .sel(controlunit_1_out_7));  // open: in2, in3
  ALU alu_1 (
    .Operand_1(multiplexer_4_out), .Operand_2(multiplexer_5_out), .ALUOper(controlunit_1_out_4),
    .ALUResultado(alu_1_aluresultado), .in_3(SftAmt));  // open: in_4, Clock
  PCControl pccontrol_1 (
    .in_1(Cycle), .in_3(alu_1_aluresultado), .in_4(Funct3), .in_5(OpCode), .PCSrc(PCWrite));  // open: in_2
  Register #(.width(32), .Select("low")) ALUOut (
    .D(alu_1_aluresultado), .Q(memorydataregister_1_out_3), .clk(Clock));  // open: en, clr
  // Probe on Cycle
  Multiplexer #(.width(32), .enable("false")) multiplexer_6 (
    .in0(memorydataregister_1_out_3), .out(multiplexer_6_out), .sel(X));  // open: in1

  // Notes on the sheet:
  //   I-Type
  //   S-Type
  //   B-Type
  //   J-Type
endmodule

module Memory (
  input  [31:0] in_1,
  input  [31:0] in_2,
  input  in_3,
  input  in_4,
  input  in_5,
  input  in_6,
  output [31:0] out_7
);

  wire not_1_out;
  wire [31:0] multiplexer_1_out, ram_1_data, rom_1_data;

  not not_1 (not_1_out, in_6);
  ROM #(.addrWidth(6), .dataWidth(32), .Select("low")) rom_1 (.addr(in_1[7:2]), .data(rom_1_data), .sel(in_6));
  Multiplexer #(.width(32), .enable("false")) multiplexer_1 (
    .in0(rom_1_data), .in1(ram_1_data), .out(multiplexer_1_out), .sel(in_6));
  RAM #(.addrWidth(6), .dataWidth(32), .bus("separate"), .Select("low")) ram_1 (
    .addr(in_1[7:2]), .din(in_2), .data(ram_1_data), .str(in_4), .sel(not_1_out), .clk(in_5));  // open: ld, clr
  assign out_7 = in_3 ? multiplexer_1_out : 32'bz;  // Controlled_Buffer controlled_buffer_1

  // Other names for the same wires on the sheet: Clock = in_5; ReadAddress[7:0] = in_1[7:0];
  //   Instruction[31:0] = out_7; IorD = in_6; MemRead = in_3; MemWrite = in_4; WriteData[31:0] = in_2
endmodule

module InstructionRegister (
  input  [31:0] in_1,
  input  in_2,
  input  in_3,
  output [4:0] out_4,
  output [6:0] out_5,
  output [4:0] out_6,
  output [2:0] out_7,
  output [4:0] out_8,
  output [31:0] out_9
);

  Register #(.width(32), .Select("low")) register_1 (
    .D(in_1), .en(in_3), .Q({out_9[31:25], out_6, out_4, out_7, out_8, out_5}), .clk(in_2));  // open: clr

  assign out_9[24:0] = {out_6, out_4, out_7, out_8, out_5};

  // Other names for the same wires on the sheet: Clock = in_2; Instructions[31:0] = in_1; IRWrite = in_3;
  //   OpCode[6:0] = out_5; Output[31:0] = {out_9[31:25], out_6, out_4, out_7, out_8, out_5}; wr[4:0] = out_8;
  //   Func3[2:0] = out_7; rs1[4:0] = out_4; rs2[4:0] = out_6
endmodule

module MemoryDataRegister (
  input  [31:0] in_1,
  input  in_2,
  output [31:0] out_3
);

  Register #(.width(32), .Select("low")) Register (.D(in_1), .Q(out_3), .clk(in_2));  // open: en, clr

  // Other names for the same wires on the sheet: Clock = in_2; Instructions[31:0] = in_1; Output[31:0] = out_3
endmodule

module RegisterFile (
  input  Clock,
  input  [4:0] ReadRegister1,
  input  [4:0] ReadRegister2,
  input  [4:0] WriteRegister,
  input  [31:0] WriteData,
  input  RegisterWrite,
  output [31:0] ReadData1,
  output [31:0] ReadData2
);

  wire and_1_out, and_2_out, and_3_out, and_4_out, and_5_out, and_6_out, and_7_out, and_8_out, and_9_out,
       and_10_out, and_11_out, and_12_out, and_13_out, and_14_out, and_15_out, and_16_out, and_17_out,
       and_18_out, and_19_out, and_20_out, and_21_out, and_22_out, and_23_out, and_24_out, and_25_out,
       and_26_out, and_27_out, and_28_out, and_29_out, and_30_out, and_31_out, and_32_out, decoder_1_out0,
       decoder_1_out1, decoder_1_out2, decoder_1_out3, decoder_1_out4, decoder_1_out5, decoder_1_out6,
       decoder_1_out7, decoder_1_out8, decoder_1_out9, decoder_1_out10, decoder_1_out11, decoder_1_out12,
       decoder_1_out13, decoder_1_out14, decoder_1_out15, decoder_1_out16, decoder_1_out17, decoder_1_out18,
       decoder_1_out19, decoder_1_out20, decoder_1_out21, decoder_1_out22, decoder_1_out23, decoder_1_out24,
       decoder_1_out25, decoder_1_out26, decoder_1_out27, decoder_1_out28, decoder_1_out29, decoder_1_out30,
       decoder_1_out31;
  wire [31:0] register_1_q, register_2_q, register_3_q, register_4_q, register_5_q, register_6_q,
       register_7_q, register_8_q, register_9_q, register_10_q, register_11_q, register_12_q, register_13_q,
       register_14_q, register_15_q, register_16_q, register_17_q, register_18_q, register_19_q,
       register_20_q, register_21_q, register_22_q, register_23_q, register_24_q, register_25_q,
       register_26_q, register_27_q, register_28_q, register_29_q, register_30_q, register_31_q,
       register_32_q;

  Decoder #(.select(5), .enable("false")) decoder_1 (
    .out0(decoder_1_out0), .out1(decoder_1_out1), .out2(decoder_1_out2), .out3(decoder_1_out3),
    .out4(decoder_1_out4), .out5(decoder_1_out5), .out6(decoder_1_out6), .out7(decoder_1_out7),
    .out8(decoder_1_out8), .out9(decoder_1_out9), .out10(decoder_1_out10), .out11(decoder_1_out11),
    .out12(decoder_1_out12), .out13(decoder_1_out13), .out14(decoder_1_out14), .out15(decoder_1_out15),
    .out16(decoder_1_out16), .out17(decoder_1_out17), .out18(decoder_1_out18), .out19(decoder_1_out19),
    .out20(decoder_1_out20), .out21(decoder_1_out21), .out22(decoder_1_out22), .out23(decoder_1_out23),
    .out24(decoder_1_out24), .out25(decoder_1_out25), .out26(decoder_1_out26), .out27(decoder_1_out27),
    .out28(decoder_1_out28), .out29(decoder_1_out29), .out30(decoder_1_out30), .out31(decoder_1_out31),
    .sel(WriteRegister));
  and and_1 (and_1_out, decoder_1_out0, RegisterWrite);
  and and_2 (and_2_out, decoder_1_out8, RegisterWrite);
  and and_3 (and_3_out, decoder_1_out16, RegisterWrite);
  and and_4 (and_4_out, decoder_1_out24, RegisterWrite);
  and and_5 (and_5_out, decoder_1_out1, RegisterWrite);
  and and_6 (and_6_out, decoder_1_out9, RegisterWrite);
  and and_7 (and_7_out, decoder_1_out17, RegisterWrite);
  and and_8 (and_8_out, decoder_1_out25, RegisterWrite);
  and and_9 (and_9_out, decoder_1_out2, RegisterWrite);
  and and_10 (and_10_out, decoder_1_out10, RegisterWrite);
  and and_11 (and_11_out, decoder_1_out18, RegisterWrite);
  and and_12 (and_12_out, decoder_1_out26, RegisterWrite);
  and and_13 (and_13_out, decoder_1_out3, RegisterWrite);
  and and_14 (and_14_out, decoder_1_out11, RegisterWrite);
  and and_15 (and_15_out, decoder_1_out19, RegisterWrite);
  and and_16 (and_16_out, decoder_1_out27, RegisterWrite);
  and and_17 (and_17_out, decoder_1_out4, RegisterWrite);
  and and_18 (and_18_out, decoder_1_out12, RegisterWrite);
  and and_19 (and_19_out, decoder_1_out20, RegisterWrite);
  and and_20 (and_20_out, decoder_1_out28, RegisterWrite);
  and and_21 (and_21_out, decoder_1_out5, RegisterWrite);
  and and_22 (and_22_out, decoder_1_out13, RegisterWrite);
  and and_23 (and_23_out, decoder_1_out21, RegisterWrite);
  and and_24 (and_24_out, decoder_1_out29, RegisterWrite);
  and and_25 (and_25_out, decoder_1_out6, RegisterWrite);
  and and_26 (and_26_out, decoder_1_out7, RegisterWrite);
  and and_27 (and_27_out, decoder_1_out14, RegisterWrite);
  and and_28 (and_28_out, decoder_1_out15, RegisterWrite);
  and and_29 (and_29_out, decoder_1_out23, RegisterWrite);
  and and_30 (and_30_out, decoder_1_out22, RegisterWrite);
  and and_31 (and_31_out, decoder_1_out30, RegisterWrite);
  and and_32 (and_32_out, decoder_1_out31, RegisterWrite);
  Register #(.width(32), .Select("low")) register_1 (
    .D(WriteData), .en(and_26_out), .Q(register_1_q), .clk(Clock));  // open: clr
  Register #(.width(32), .Select("low")) register_2 (
    .D(WriteData), .en(and_28_out), .Q(register_2_q), .clk(Clock));  // open: clr
  Register #(.width(32), .Select("low")) register_3 (
    .D(WriteData), .en(and_29_out), .Q(register_3_q), .clk(Clock));  // open: clr
  Register #(.width(32), .Select("low")) register_4 (
    .D(WriteData), .en(and_32_out), .Q(register_4_q), .clk(Clock));  // open: clr
  Register #(.width(32), .Select("low")) register_5 (
    .D(WriteData), .en(and_25_out), .Q(register_5_q), .clk(Clock));  // open: clr
  Register #(.width(32), .Select("low")) register_6 (
    .D(WriteData), .en(and_27_out), .Q(register_6_q), .clk(Clock));  // open: clr
  Register #(.width(32), .Select("low")) register_7 (
    .D(WriteData), .en(and_30_out), .Q(register_7_q), .clk(Clock));  // open: clr
  Register #(.width(32), .Select("low")) register_8 (
    .D(WriteData), .en(and_31_out), .Q(register_8_q), .clk(Clock));  // open: clr
  Register #(.width(32), .Select("low")) register_9 (
    .D(WriteData), .en(and_21_out), .Q(register_9_q), .clk(Clock));  // open: clr
  Register #(.width(32), .Select("low")) register_10 (
    .D(WriteData), .en(and_22_out), .Q(register_10_q), .clk(Clock));  // open: clr
  Register #(.width(32), .Select("low")) register_11 (
    .D(WriteData), .en(and_23_out), .Q(register_11_q), .clk(Clock));  // open: clr
  Register #(.width(32), .Select("low")) register_12 (
    .D(WriteData), .en(and_24_out), .Q(register_12_q), .clk(Clock));  // open: clr
  Register #(.width(32), .Select("low")) register_13 (
    .D(WriteData), .en(and_17_out), .Q(register_13_q), .clk(Clock));  // open: clr
  Register #(.width(32), .Select("low")) register_14 (
    .D(WriteData), .en(and_18_out), .Q(register_14_q), .clk(Clock));  // open: clr
  Register #(.width(32), .Select("low")) register_15 (
    .D(WriteData), .en(and_19_out), .Q(register_15_q), .clk(Clock));  // open: clr
  Register #(.width(32), .Select("low")) register_16 (
    .D(WriteData), .en(and_20_out), .Q(register_16_q), .clk(Clock));  // open: clr
  Register #(.width(32), .Select("low")) register_17 (
    .D(WriteData), .en(and_13_out), .Q(register_17_q), .clk(Clock));  // open: clr
  Register #(.width(32), .Select("low")) register_18 (
    .D(WriteData), .en(and_14_out), .Q(register_18_q), .clk(Clock));  // open: clr
  Register #(.width(32), .Select("low")) register_19 (
    .D(WriteData), .en(and_15_out), .Q(register_19_q), .clk(Clock));  // open: clr
  Register #(.width(32), .Select("low")) register_20 (
    .D(WriteData), .en(and_16_out), .Q(register_20_q), .clk(Clock));  // open: clr
  Register #(.width(32), .Select("low")) register_21 (
    .D(WriteData), .en(and_9_out), .Q(register_21_q), .clk(Clock));  // open: clr
  Register #(.width(32), .Select("low")) register_22 (
    .D(WriteData), .en(and_10_out), .Q(register_22_q), .clk(Clock));  // open: clr
  Register #(.width(32), .Select("low")) register_23 (
    .D(WriteData), .en(and_11_out), .Q(register_23_q), .clk(Clock));  // open: clr
  Register #(.width(32), .Select("low")) register_24 (
    .D(WriteData), .en(and_12_out), .Q(register_24_q), .clk(Clock));  // open: clr
  Register #(.width(32), .Select("low")) register_25 (
    .D(WriteData), .en(and_5_out), .Q(register_25_q), .clk(Clock));  // open: clr
  Register #(.width(32), .Select("low")) register_26 (
    .D(WriteData), .en(and_6_out), .Q(register_26_q), .clk(Clock));  // open: clr
  Register #(.width(32), .Select("low")) register_27 (
    .D(WriteData), .en(and_7_out), .Q(register_27_q), .clk(Clock));  // open: clr
  Register #(.width(32), .Select("low")) register_28 (
    .D(WriteData), .en(and_8_out), .Q(register_28_q), .clk(Clock));  // open: clr
  Register #(.width(32), .Select("low")) register_29 (
    .D(WriteData), .en(and_1_out), .Q(register_29_q), .clk(Clock));  // open: clr
  Register #(.width(32), .Select("low")) register_30 (
    .D(WriteData), .en(and_2_out), .Q(register_30_q), .clk(Clock));  // open: clr
  Register #(.width(32), .Select("low")) register_31 (
    .D(WriteData), .en(and_3_out), .Q(register_31_q), .clk(Clock));  // open: clr
  Register #(.width(32), .Select("low")) register_32 (
    .D(WriteData), .en(and_4_out), .Q(register_32_q), .clk(Clock));  // open: clr
  Multiplexer #(.select(5), .width(32), .enable("false")) multiplexer_1 (
    .in0(register_1_q), .in1(register_5_q), .in2(register_9_q), .in3(register_13_q), .in4(register_17_q),
    .in5(register_21_q), .in6(register_25_q), .in7(register_29_q), .in8(register_2_q), .in9(register_6_q),
    .in10(register_10_q), .in11(register_14_q), .in12(register_18_q), .in13(register_22_q),
    .in14(register_26_q), .in15(register_30_q), .in16(register_3_q), .in17(register_7_q),
    .in18(register_11_q), .in19(register_15_q), .in20(register_19_q), .in21(register_23_q),
    .in22(register_27_q), .in23(register_31_q), .in24(register_4_q), .in25(register_8_q),
    .in26(register_12_q), .in27(register_16_q), .in28(register_20_q), .in29(register_24_q),
    .in30(register_28_q), .in31(register_32_q), .out(ReadData1), .sel(ReadRegister1));
  Multiplexer #(.select(5), .width(32), .enable("false")) multiplexer_2 (
    .in0(register_1_q), .in1(register_5_q), .in2(register_9_q), .in3(register_13_q), .in4(register_17_q),
    .in5(register_21_q), .in6(register_25_q), .in7(register_29_q), .in8(register_2_q), .in9(register_6_q),
    .in10(register_10_q), .in11(register_14_q), .in12(register_18_q), .in13(register_22_q),
    .in14(register_26_q), .in15(register_30_q), .in16(register_3_q), .in17(register_7_q),
    .in18(register_11_q), .in19(register_15_q), .in20(register_19_q), .in21(register_23_q),
    .in22(register_27_q), .in23(register_31_q), .in24(register_4_q), .in25(register_8_q),
    .in26(register_12_q), .in27(register_16_q), .in28(register_20_q), .in29(register_24_q),
    .in30(register_28_q), .in31(register_32_q), .out(ReadData2), .sel(ReadRegister2));

  // Notes on the sheet:
  //   Entradas
  //   Control
  //   Salidas
endmodule

module ALU (
  input  [31:0] Operand_1,
  input  [31:0] Operand_2,
  input  [4:0] in_3,
  input  in_4,
  input  [3:0] ALUOper,
  input  Clock,
  output [31:0] ALUResultado
);

  wire [31:0] adder_1_out, and_1_out, multiplexer_1_out, multiplexer_2_out, or_1_out, shifter_1_out,
       shifter_2_out, shifter_3_out, shifter_4_out, shifter_5_out, subtractor_1_out, xor_1_out;

  Adder #(.width(32)) adder_1 (.a(Operand_1), .b(Operand_2), .out(adder_1_out));  // open: cin, cout
  Subtractor #(.width(32)) subtractor_1 (.a(Operand_1), .b(Operand_2), .out(subtractor_1_out));  // open: bin, bout
  Shifter #(.width(32)) shifter_1 (.in(Operand_1), .\dist (Operand_2[4:0]), .out(shifter_1_out));
  Multiplexer #(.width(32), .enable("false")) multiplexer_1 (
    .in0(adder_1_out), .in1(subtractor_1_out), .out(multiplexer_1_out), .sel(ALUOper[3]));
  Comparator #(.width(32)) comparator_1 (.a({32{1'b0}}), .b(subtractor_1_out), .eq(in_4));  // open: gt, lt
  Shifter #(.width(32)) shifter_2 (.in(Operand_1), .\dist (Operand_2[4:0]), .out(shifter_2_out));
  Shifter #(.width(32)) shifter_3 (.in(Operand_1), .\dist (Operand_2[4:0]), .out(shifter_3_out));
  Shifter #(.width(32), .shift("lr")) shifter_4 (.in(Operand_1), .\dist (Operand_2[4:0]), .out(shifter_4_out));
  Shifter #(.width(32), .shift("ar")) shifter_5 (.in(Operand_1), .\dist (Operand_2[4:0]), .out(shifter_5_out));
  assign xor_1_out = Operand_1 ^ Operand_2;  // XOR_Gate xor_1, 32 bits wide
  Multiplexer #(.width(32), .enable("false")) multiplexer_2 (
    .in0(shifter_4_out), .in1(shifter_5_out), .out(multiplexer_2_out), .sel(ALUOper[3]));
  assign or_1_out = Operand_1 | Operand_2;  // OR_Gate or_1, 32 bits wide
  assign and_1_out = Operand_1 & Operand_2;  // AND_Gate and_1, 32 bits wide
  Multiplexer #(.select(3), .width(32), .enable("false")) multiplexer_3 (
    .in0(multiplexer_1_out), .in1(shifter_1_out), .in2(shifter_2_out), .in3(shifter_3_out), .in4(xor_1_out),
    .in5(multiplexer_2_out), .in6(or_1_out), .in7(and_1_out), .out(ALUResultado), .sel(ALUOper[2:0]));

  // Other names for the same wires on the sheet: Input1[31:0] = Operand_1; Input2[31:0] = Operand_2;
  //   SftAmt[4:0] = in_3; Zero = in_4

  // Notes on the sheet:
  //   ADD
  //   SUB
  //   SLL
  //   SLT
  //   SLTU
  //   SRL
  //   SRA
endmodule

module ControlUnit (
  input  in_1,
  input  [31:0] in_2,
  output [1:0] out_3,
  output [3:0] out_4,
  output [2:0] out_5,
  output out_6,
  output [1:0] out_7,
  output out_8,
  output out_9,
  output out_10,
  output out_11,
  output out_12,
  output out_13
);

  wire and_1_out, and_2_out, B, comparator_1_eq, comparator_2_eq, I, J, or_1_out, or_2_out, or_5_out,
       or_6_out, or_7_out, R, Reset;
  wire [3:0] ALUO;
  wire [5:1] Cycle3;
  wire [10:6] Cycle2;
  wire [14:0] controlled_buffer_1_out;

  and u_R (R, in_2[0], in_2[1], ~in_2[2], ~in_2[3], in_2[4], in_2[5], ~in_2[6]);  // AND_Gate
  and u_I (I, in_2[0], in_2[1], ~in_2[2], ~in_2[3], in_2[4], ~in_2[5], ~in_2[6]);  // AND_Gate
  and LW (Cycle3[4], in_2[0], in_2[1], ~in_2[2], ~in_2[3], ~in_2[4], ~in_2[5], ~in_2[6]);  // AND_Gate
  and SW (Cycle3[2], in_2[0], in_2[1], ~in_2[2], ~in_2[3], ~in_2[4], in_2[5], ~in_2[6]);  // AND_Gate
  and u_B (B, in_2[0], in_2[1], ~in_2[2], ~in_2[3], ~in_2[4], in_2[5], in_2[6]);  // AND_Gate
  and u_J (J, in_2[0], in_2[1], in_2[2], in_2[3], ~in_2[4], in_2[5], in_2[6]);  // AND_Gate
  assign controlled_buffer_1_out = J ? 15'h2c0 : 15'bz;  // Controlled_Buffer controlled_buffer_1
  assign controlled_buffer_1_out = ~J ? 15'h280 : 15'bz;  // Controlled_Buffer controlled_buffer_2
  Counter #(.width(3), .max('h4), .trigger("falling")) counter_1 (
    .Q(out_5), .clk(in_1), .clr(Reset));  // open: load, D, count, carry, preset, down
  Multiplexer #(.select(3), .width(15), .enable("false")) multiplexer_1 (
    .in0(15'h111), .in1(controlled_buffer_1_out), .in2({ALUO, Cycle2, {6{1'b0}}}),
    .in3({ALUO, {5{1'b0}}, Cycle3[5:4], 1'b0, Cycle3[2:1], 1'b0}), .in4(15'ha),
    .out({out_4, out_6, out_7, out_3, out_8, out_10, out_13, out_11, out_12, out_9}), .sel(out_5));  // open: in5, in6, in7
  // Probe on out_5
  Comparator #(.width(3)) comparator_1 (.a(out_5), .b(3'b011), .eq(comparator_1_eq));  // open: gt, lt
  Comparator #(.width(3)) comparator_2 (.a(out_5), .b(3'b100), .eq(comparator_2_eq));  // open: gt, lt
  or or_1 (or_1_out, B, J);
  or or_2 (or_2_out, I, Cycle3[2], R);
  and and_1 (and_1_out, or_1_out, comparator_1_eq);
  or or_3 (Reset, and_1_out, and_2_out);
  and and_2 (and_2_out, or_2_out, comparator_2_eq);
  or or_4 (Cycle2[10], R, I, B, Cycle3[4], Cycle3[2]);
  or or_5 (or_5_out, R, I);
  assign Cycle2[9:8] = ~or_6_out ? 2'b00 : 2'bz;  // Controlled_Buffer controlled_buffer_3
  assign Cycle2[9:8] = or_6_out ? 2'b10 : 2'bz;  // Controlled_Buffer controlled_buffer_4
  or or_6 (or_6_out, I, Cycle3[4], Cycle3[2]);
  assign ALUO = or_5_out ? {in_2[14:12], in_2[30]} : 4'bz;  // Controlled_Buffer controlled_buffer_5
  or or_7 (or_7_out, Cycle3[4], Cycle3[2], J);
  assign Cycle2[7:6] = ~Cycle3[2] ? 2'b00 : 2'bz;  // Controlled_Buffer controlled_buffer_6
  assign Cycle2[7:6] = Cycle3[2] ? 2'b01 : 2'bz;  // Controlled_Buffer controlled_buffer_7
  or or_8 (Cycle3[5], Cycle3[4], Cycle3[2]);
  or or_9 (Cycle3[1], R, I);
  assign ALUO = or_7_out ? 4'b0000 : 4'bz;  // Controlled_Buffer controlled_buffer_8
  assign ALUO = B ? 4'b1000 : 4'bz;  // Controlled_Buffer controlled_buffer_9

  // Other names for the same wires on the sheet: IRWrite = out_9; RegWrite = out_12; MemWrite = out_11;
  //   MemToReg = out_13; MemRead = out_10; IorD = out_8; Imm[1:0] = out_3; ALUSrcB[1:0] = out_7; ALUSrcA = out_6;
  //   ALUOp[3:0] = out_4; Funct7[6:0] = in_2[31:25]; Instructions[31:0] = in_2; Funct3[2:0] = in_2[14:12];
  //   Clock = in_1; Cycle[2:0] = out_5; Cycle2[14:11] = ALUO; Cycle3[14:11] = ALUO; SW = Cycle3[2]; LW = Cycle3[4];
  //   OpCode[6:0] = in_2[6:0]
endmodule

module PCControl (
  input  [2:0] in_1,
  input  in_2,
  input  [31:0] in_3,
  input  [2:0] in_4,
  input  [6:0] in_5,
  output PCSrc
);

  wire and_1_out, BEQ_out, BGE_out, BGEL_out, BLT_out, BLTU_out, BNE_out, comparator_1_eq, comparator_1_gt,
       comparator_1_lt, comparator_2_eq, comparator_2_gt, comparator_2_lt, comparator_3_eq, comparator_4_eq,
       decoder_1_out1, decoder_1_out2, demultiplexer_1_out0, demultiplexer_1_out1, demultiplexer_1_out4,
       demultiplexer_1_out5, demultiplexer_1_out6, demultiplexer_1_out7, IsBranch_out, multiplexer_1_out,
       not_1_out, or_1_out, or_2_out, or_3_out;

  Demultiplexer #(.select(3), .enable("false")) demultiplexer_1 (
    .out0(demultiplexer_1_out0), .out1(demultiplexer_1_out1), .out4(demultiplexer_1_out4),
    .out5(demultiplexer_1_out5), .out6(demultiplexer_1_out6), .out7(demultiplexer_1_out7), .in(1'b1),
    .sel(in_4));  // open: out2, out3
  Comparator #(.width(32)) comparator_1 (
    .a(in_3), .b({32{1'b0}}), .gt(comparator_1_gt), .eq(comparator_1_eq), .lt(comparator_1_lt));
  Comparator #(.width(32)) comparator_2 (
    .a(in_3), .b({32{1'b0}}), .gt(comparator_2_gt), .eq(comparator_2_eq), .lt(comparator_2_lt));
  not not_1 (not_1_out, comparator_1_eq);
  or or_1 (or_1_out, comparator_1_eq, comparator_1_gt);
  or or_2 (or_2_out, comparator_2_gt, comparator_2_eq);
  and BEQ (BEQ_out, comparator_1_eq, demultiplexer_1_out0);
  and BNE (BNE_out, demultiplexer_1_out1, not_1_out);
  and BLT (BLT_out, demultiplexer_1_out4, comparator_1_lt);
  and BGE (BGE_out, demultiplexer_1_out5, or_1_out);
  and BLTU (BLTU_out, demultiplexer_1_out6, comparator_2_lt);
  and BGEL (BGEL_out, demultiplexer_1_out7, or_2_out);
  Multiplexer #(.select(3), .enable("false")) multiplexer_1 (
    .in0(BEQ_out), .in1(BNE_out), .in4(BLT_out), .in5(BGE_out), .in6(BLTU_out), .in7(BGEL_out),
    .out(multiplexer_1_out), .sel(in_4));  // open: in2, in3
  Comparator #(.width(7)) comparator_3 (.a(in_5), .b(7'b1101111), .eq(comparator_3_eq));  // open: gt, lt
  Comparator #(.width(7)) comparator_4 (.a(in_5), .b(7'b1100011), .eq(comparator_4_eq));  // open: gt, lt
  Decoder #(.select(3), .enable("false")) decoder_1 (
    .out1(decoder_1_out1), .out2(decoder_1_out2), .sel(in_1));  // open: out0, out3, out4, out5, out6, out7
  and IsBranch (IsBranch_out, comparator_4_eq, decoder_1_out2, multiplexer_1_out);
  and and_1 (and_1_out, comparator_3_eq, decoder_1_out2);
  or or_3 (or_3_out, IsBranch_out, and_1_out);
  or or_4 (PCSrc, or_3_out, decoder_1_out1);

  // Other names for the same wires on the sheet: ALUResult[31:0] = in_3; Clock = in_2; Cycle[2:0] = in_1;
  //   Func3[2:0] = in_4; OpCode[6:0] = in_5
endmodule
