// Logisim project pipelined-layout.circ as structural Verilog
module main (
);

  wire undriven_6;
  wire [31:0] adder_1_out, adder_2_out, alu_1_aluresultado, bit_extender_1_out, bit_extender_2_out,
       bit_extender_3_out, bit_extender_4_out, Instruction_Memory_data, memory_1_out_7, multiplexer_1_out,
       multiplexer_2_out, multiplexer_3_out, PC_q, registerfile_1_readdata1, registerfile_1_readdata2,
       undriven, undriven_3, undriven_4, undriven_5, undriven_7, undriven_8, undriven_9, undriven_10;
  wire [31:7] undriven_2;

  Multiplexer #(.width(32), .enable("false")) multiplexer_1 (
    .in0(adder_1_out), .in1(undriven), .out(multiplexer_1_out));  // open: sel
  Register #(.width(32), .Select("low")) PC (.D(multiplexer_1_out), .Q(PC_q));  // open: en, clk, clr
  Adder #(.width(32)) adder_1 (.a(32'h4), .b(PC_q), .out(adder_1_out));  // open: cin, cout
  ROM #(.dataWidth(32), .Select("low")) Instruction_Memory (.addr(PC_q[9:2]), .data(Instruction_Memory_data));
  IF_ID if_id_1 ();
  RegisterFile registerfile_1 (
    .ReadRegister1(undriven_2[24:20]), .ReadRegister2(undriven_2[19:15]), .WriteData(multiplexer_3_out),
    .ReadData1(registerfile_1_readdata1), .ReadData2(registerfile_1_readdata2));  // open: Clock, WriteRegister, RegisterWrite
  assign bit_extender_1_out = {{20{undriven_2[31]}}, undriven_2[31:20]};  // Bit_Extender bit_extender_1
  assign bit_extender_2_out = {{20{undriven_2[31]}}, {undriven_2[31:25], undriven_2[11:7]}};  // Bit_Extender bit_extender_2
  assign bit_extender_3_out = {{11{undriven_2[31]}}, {undriven_2[31], undriven_2[19:12], undriven_2[20], undriven_2[30:21], 1'b0}};  // Bit_Extender bit_extender_3
  assign bit_extender_4_out = {{19{undriven_2[31]}}, {undriven_2[31], undriven_2[7], undriven_2[30:25], undriven_2[11:8], 1'b0}};  // Bit_Extender bit_extender_4
  ID_EX id_ex_1 ();
  Adder #(.width(32)) adder_2 (.out(adder_2_out));  // open: a, b, cin, cout
  ALU alu_1 (
    .Operand_1(undriven_3), .Operand_2(multiplexer_2_out), .ALUResultado(alu_1_aluresultado),
    .in_4(undriven_6));  // open: ALUOper, Clock, in_3
  Multiplexer #(.width(32), .enable("false")) multiplexer_2 (
    .in0(undriven_4), .in1(undriven_5), .out(multiplexer_2_out));  // open: sel
  EX_MEM ex_mem_1 ();
  Memory memory_1 (.in_1(undriven_7), .out_7(memory_1_out_7), .in_2(undriven_8));  // open: in_3, in_4, in_5, in_6
  MEM_WB mem_wb_1 ();
  Multiplexer #(.width(32), .enable("false")) multiplexer_3 (
    .in0(undriven_9), .in1(undriven_10), .out(multiplexer_3_out));  // open: sel

  // Notes on the sheet:
  //   contents of Instruction_Memory (hex, n*v repeats v):
  //   211020 a21820 462020 842820 ac850080
  //   SW
  //   Jump
  //   Branch
endmodule

module Memory (
  input  [31:0] in_1,
  input  [31:0] in_2,
  input  in_3,
  input  in_4,
  input  in_5,
  input  in_6,
  output [31:0] out_7
);

  wire not_1_out;
  wire [31:0] multiplexer_1_out, ram_1_data, rom_1_data;

  not not_1 (not_1_out, in_6);
  ROM #(.dataWidth(32), .Select("low")) rom_1 (.addr(in_1[7:0]), .data(rom_1_data), .sel(in_6));
  Multiplexer #(.width(32), .enable("false")) multiplexer_1 (
    .in0(rom_1_data), .in1(ram_1_data), .out(multiplexer_1_out), .sel(in_6));
  RAM #(.dataWidth(32), .bus("separate"), .simpleMode("false"), .Select("low")) ram_1 (
    .addr(in_1[7:0]), .din(in_2), .data(ram_1_data), .str(in_4), .sel(not_1_out), .clk(in_5));  // open: ld, clr
  assign out_7 = in_3 ? multiplexer_1_out : 32'bz;  // Controlled_Buffer controlled_buffer_1

  // Other names for the same wires on the sheet: Clock = in_5; ReadAddress[7:0] = in_1[7:0];
  //   Instruction[31:0] = out_7; IorD = in_6; MemRead = in_3; MemWrite = in_4; WriteData[31:0] = in_2
endmodule

module InstructionRegister (
  input  [31:0] in_1,
  input  in_2,
  input  in_3,
  output [4:0] out_4,
  output [6:0] out_5,
  output [4:0] out_6,
  output [2:0] out_7,
  output [4:0] out_8,
  output [31:0] out_9
);

  Register #(.width(32), .Select("low")) register_1 (
    .D(in_1), .en(in_3), .Q({out_9[31:25], out_6, out_4, out_7, out_8, out_5}), .clk(in_2));  // open: clr

  assign out_9[24:0] = {out_6, out_4, out_7, out_8, out_5};

  // Other names for the same wires on the sheet: Clock = in_2; Instructions[31:0] = in_1; IRWrite = in_3;
  //   OpCode[6:0] = out_5; Output[31:0] = {out_9[31:25], out_6, out_4, out_7, out_8, out_5}; wr[4:0] = out_8;
  //   Func3[2:0] = out_7; rs1[4:0] = out_4; rs2[4:0] = out_6
endmodule

module MemoryDataRegister (
  input  [31:0] in_1,
  input  in_2,
  output [31:0] out_3
);

  Register #(.width(32), .Select("low")) Register (.D(in_1), .Q(out_3), .clk(in_2));  // open: en, clr

  // Other names for the same wires on the sheet: Clock = in_2; Instructions[31:0] = in_1; Output[31:0] = out_3
endmodule

module RegisterFile (
  input  Clock,
  input  [4:0] ReadRegister1,
  input  [4:0] ReadRegister2,
  input  [4:0] WriteRegister,
  input  [31:0] WriteData,
  input  RegisterWrite,
  output [31:0] ReadData1,
  output [31:0] ReadData2
);

  wire and_1_out, and_2_out, and_3_out, and_4_out, and_5_out, and_6_out, and_7_out, and_8_out, and_9_out,
       and_10_out, and_11_out, and_12_out, and_13_out, and_14_out, and_15_out, and_16_out, and_17_out,
       and_18_out, and_19_out, and_20_out, and_21_out, and_22_out, and_23_out, and_24_out, and_25_out,
       and_26_out, and_27_out, and_28_out, and_29_out, and_30_out, and_31_out, and_32_out, decoder_1_out0,
       decoder_1_out1, decoder_1_out2, decoder_1_out3, decoder_1_out4, decoder_1_out5, decoder_1_out6,
       decoder_1_out7, decoder_1_out8, decoder_1_out9, decoder_1_out10, decoder_1_out11, decoder_1_out12,
       decoder_1_out13, decoder_1_out14, decoder_1_out15, decoder_1_out16, decoder_1_out17, decoder_1_out18,
       decoder_1_out19, decoder_1_out20, decoder_1_out21, decoder_1_out22, decoder_1_out23, decoder_1_out24,
       decoder_1_out25, decoder_1_out26, decoder_1_out27, decoder_1_out28, decoder_1_out29, decoder_1_out30,
       decoder_1_out31;
  wire [31:0] register_1_q, register_2_q, register_3_q, register_4_q, register_5_q, register_6_q,
       register_7_q, register_8_q, register_9_q, register_10_q, register_11_q, register_12_q, register_13_q,
       register_14_q, register_15_q, register_16_q, register_17_q, register_18_q, register_19_q,
       register_20_q, register_21_q, register_22_q, register_23_q, register_24_q, register_25_q,
       register_26_q, register_27_q, register_28_q, register_29_q, register_30_q, register_31_q,
       register_32_q;

  Decoder #(.select(5), .enable("false")) decoder_1 (
    .out0(decoder_1_out0), .out1(decoder_1_out1), .out2(decoder_1_out2), .out3(decoder_1_out3),
    .out4(decoder_1_out4), .out5(decoder_1_out5), .out6(decoder_1_out6), .out7(decoder_1_out7),
    .out8(decoder_1_out8), .out9(decoder_1_out9), .out10(decoder_1_out10), .out11(decoder_1_out11),
    .out12(decoder_1_out12), .out13(decoder_1_out13), .out14(decoder_1_out14), .out15(decoder_1_out15),
    .out16(decoder_1_out16), .out17(decoder_1_out17), .out18(decoder_1_out18), .out19(decoder_1_out19),
    .out20(decoder_1_out20), .out21(decoder_1_out21), .out22(decoder_1_out22), .out23(decoder_1_out23),
    .out24(decoder_1_out24), .out25(decoder_1_out25), .out26(decoder_1_out26), .out27(decoder_1_out27),
    .out28(decoder_1_out28), .out29(decoder_1_out29), .out30(decoder_1_out30), .out31(decoder_1_out31),
    .sel(WriteRegister));
  and and_1 (and_1_out, decoder_1_out0, RegisterWrite);
  and and_2 (and_2_out, decoder_1_out8, RegisterWrite);
  and and_3 (and_3_out, decoder_1_out16, RegisterWrite);
  and and_4 (and_4_out, decoder_1_out24, RegisterWrite);
  and and_5 (and_5_out, decoder_1_out1, RegisterWrite);
  and and_6 (and_6_out, decoder_1_out9, RegisterWrite);
  and and_7 (and_7_out, decoder_1_out17, RegisterWrite);
  and and_8 (and_8_out, decoder_1_out25, RegisterWrite);
  and and_9 (and_9_out, decoder_1_out2, RegisterWrite);
  and and_10 (and_10_out, decoder_1_out10, RegisterWrite);
  and and_11 (and_11_out, decoder_1_out18, RegisterWrite);
  and and_12 (and_12_out, decoder_1_out26, RegisterWrite);
  and and_13 (and_13_out, decoder_1_out3, RegisterWrite);
  and and_14 (and_14_out, decoder_1_out11, RegisterWrite);
  and and_15 (and_15_out, decoder_1_out19, RegisterWrite);
  and and_16 (and_16_out, decoder_1_out27, RegisterWrite);
  and and_17 (and_17_out, decoder_1_out4, RegisterWrite);
  and and_18 (and_18_out, decoder_1_out12, RegisterWrite);
  and and_19 (and_19_out, decoder_1_out20, RegisterWrite);
  and and_20 (and_20_out, decoder_1_out28, RegisterWrite);
  and and_21 (and_21_out, decoder_1_out5, RegisterWrite);
  and and_22 (and_22_out, decoder_1_out13, RegisterWrite);
  and and_23 (and_23_out, decoder_1_out21, RegisterWrite);
  and and_24 (and_24_out, decoder_1_out29, RegisterWrite);
  and and_25 (and_25_out, decoder_1_out7, RegisterWrite);
  and and_26 (and_26_out, decoder_1_out6, RegisterWrite);
  and and_27 (and_27_out, decoder_1_out15, RegisterWrite);
  and and_28 (and_28_out, decoder_1_out14, RegisterWrite);
  and and_29 (and_29_out, decoder_1_out22, RegisterWrite);
  and and_30 (and_30_out, decoder_1_out23, RegisterWrite);
  and and_31 (and_31_out, decoder_1_out31, RegisterWrite);
  and and_32 (and_32_out, decoder_1_out30, RegisterWrite);
  Register #(.width(32), .Select("low")) register_1 (
    .D(WriteData), .en(and_25_out), .Q(register_1_q), .clk(Clock));  // open: clr
  Register #(.width(32), .Select("low")) register_2 (
    .D(WriteData), .en(and_27_out), .Q(register_2_q), .clk(Clock));  // open: clr
  Register #(.width(32), .Select("low")) register_3 (
    .D(WriteData), .en(and_30_out), .Q(register_3_q), .clk(Clock));  // open: clr
  Register #(.width(32), .Select("low")) register_4 (
    .D(WriteData), .en(and_31_out), .Q(register_4_q), .clk(Clock));  // open: clr
  Register #(.width(32), .Select("low")) register_5 (
    .D(WriteData), .en(and_26_out), .Q(register_5_q), .clk(Clock));  // open: clr
  Register #(.width(32), .Select("low")) register_6 (
    .D(WriteData), .en(and_28_out), .Q(register_6_q), .clk(Clock));  // open: clr
  Register #(.width(32), .Select("low")) register_7 (
    .D(WriteData), .en(and_29_out), .Q(register_7_q), .clk(Clock));  // open: clr
  Register #(.width(32), .Select("low")) register_8 (
    .D(WriteData), .en(and_32_out), .Q(register_8_q), .clk(Clock));  // open: clr
  Register #(.width(32), .Select("low")) register_9 (
    .D(WriteData), .en(and_21_out), .Q(register_9_q), .clk(Clock));  // open: clr
  Register #(.width(32), .Select("low")) register_10 (
    .D(WriteData), .en(and_22_out), .Q(register_10_q), .clk(Clock));  // open: clr
  Register #(.width(32), .Select("low")) register_11 (
    .D(WriteData), .en(and_23_out), .Q(register_11_q), .clk(Clock));  // open: clr
  Register #(.width(32), .Select("low")) register_12 (
    .D(WriteData), .en(and_24_out), .Q(register_12_q), .clk(Clock));  // open: clr
  Register #(.width(32), .Select("low")) register_13 (
    .D(WriteData), .en(and_17_out), .Q(register_13_q), .clk(Clock));  // open: clr
  Register #(.width(32), .Select("low")) register_14 (
    .D(WriteData), .en(and_18_out), .Q(register_14_q), .clk(Clock));  // open: clr
  Register #(.width(32), .Select("low")) register_15 (
    .D(WriteData), .en(and_19_out), .Q(register_15_q), .clk(Clock));  // open: clr
  Register #(.width(32), .Select("low")) register_16 (
    .D(WriteData), .en(and_20_out), .Q(register_16_q), .clk(Clock));  // open: clr
  Register #(.width(32), .Select("low")) register_17 (
    .D(WriteData), .en(and_13_out), .Q(register_17_q), .clk(Clock));  // open: clr
  Register #(.width(32), .Select("low")) register_18 (
    .D(WriteData), .en(and_14_out), .Q(register_18_q), .clk(Clock));  // open: clr
  Register #(.width(32), .Select("low")) register_19 (
    .D(WriteData), .en(and_15_out), .Q(register_19_q), .clk(Clock));  // open: clr
  Register #(.width(32), .Select("low")) register_20 (
    .D(WriteData), .en(and_16_out), .Q(register_20_q), .clk(Clock));  // open: clr
  Register #(.width(32), .Select("low")) register_21 (
    .D(WriteData), .en(and_9_out), .Q(register_21_q), .clk(Clock));  // open: clr
  Register #(.width(32), .Select("low")) register_22 (
    .D(WriteData), .en(and_10_out), .Q(register_22_q), .clk(Clock));  // open: clr
  Register #(.width(32), .Select("low")) register_23 (
    .D(WriteData), .en(and_11_out), .Q(register_23_q), .clk(Clock));  // open: clr
  Register #(.width(32), .Select("low")) register_24 (
    .D(WriteData), .en(and_12_out), .Q(register_24_q), .clk(Clock));  // open: clr
  Register #(.width(32), .Select("low")) register_25 (
    .D(WriteData), .en(and_5_out), .Q(register_25_q), .clk(Clock));  // open: clr
  Register #(.width(32), .Select("low")) register_26 (
    .D(WriteData), .en(and_6_out), .Q(register_26_q), .clk(Clock));  // open: clr
  Register #(.width(32), .Select("low")) register_27 (
    .D(WriteData), .en(and_7_out), .Q(register_27_q), .clk(Clock));  // open: clr
  Register #(.width(32), .Select("low")) register_28 (
    .D(WriteData), .en(and_8_out), .Q(register_28_q), .clk(Clock));  // open: clr
  Register #(.width(32), .Select("low")) register_29 (
    .D(WriteData), .en(and_1_out), .Q(register_29_q), .clk(Clock));  // open: clr
  Register #(.width(32), .Select("low")) register_30 (
    .D(WriteData), .en(and_2_out), .Q(register_30_q), .clk(Clock));  // open: clr
  Register #(.width(32), .Select("low")) register_31 (
    .D(WriteData), .en(and_3_out), .Q(register_31_q), .clk(Clock));  // open: clr
  Register #(.width(32), .Select("low")) register_32 (
    .D(WriteData), .en(and_4_out), .Q(register_32_q), .clk(Clock));  // open: clr
  Multiplexer #(.select(5), .width(32), .enable("false")) multiplexer_1 (
    .in0(register_1_q), .in1(register_5_q), .in2(register_9_q), .in3(register_13_q), .in4(register_17_q),
    .in5(register_21_q), .in6(register_25_q), .in7(register_29_q), .in8(register_2_q), .in9(register_6_q),
    .in10(register_10_q), .in11(register_14_q), .in12(register_18_q), .in13(register_22_q),
    .in14(register_26_q), .in15(register_30_q), .in16(register_3_q), .in17(register_7_q),
    .in18(register_11_q), .in19(register_15_q), .in20(register_19_q), .in21(register_23_q),
    .in22(register_27_q), .in23(register_31_q), .in24(register_4_q), .in25(register_8_q),
    .in26(register_12_q), .in27(register_16_q), .in28(register_20_q), .in29(register_24_q),
    .in30(register_28_q), .in31(register_32_q), .out(ReadData1), .sel(ReadRegister1));
  Multiplexer #(.select(5), .width(32), .enable("false")) multiplexer_2 (
    .in0(register_1_q), .in1(register_5_q), .in2(register_9_q), .in3(register_13_q), .in4(register_17_q),
    .in5(register_21_q), .in6(register_25_q), .in7(register_29_q), .in8(register_2_q), .in9(register_6_q),
    .in10(register_10_q), .in11(register_14_q), .in12(register_18_q), .in13(register_22_q),
    .in14(register_26_q), .in15(register_30_q), .in16(register_3_q), .in17(register_7_q),
    .in18(register_11_q), .in19(register_15_q), .in20(register_19_q), .in21(register_23_q),
    .in22(register_27_q), .in23(register_31_q), .in24(register_4_q), .in25(register_8_q),
    .in26(register_12_q), .in27(register_16_q), .in28(register_20_q), .in29(register_24_q),
    .in30(register_28_q), .in31(register_32_q), .out(ReadData2), .sel(ReadRegister2));

  // Notes on the sheet:
  //   Entradas
  //   Control
  //   Salidas
endmodule

module ALU (
  input  [31:0] Operand_1,
  input  [31:0] Operand_2,
  input  [4:0] in_3,
  input  in_4,
  input  [3:0] ALUOper,
  input  Clock,
  output [31:0] ALUResultado
);

  wire [31:0] adder_1_out, and_1_out, multiplexer_1_out, multiplexer_2_out, or_1_out, shifter_1_out,
       shifter_2_out, shifter_3_out, shifter_4_out, shifter_5_out, subtractor_1_out, xor_1_out;

  Adder #(.width(32)) adder_1 (.a(Operand_1), .b(Operand_2), .out(adder_1_out));  // open: cin, cout
  Subtractor #(.width(32)) subtractor_1 (.a(Operand_1), .b(Operand_2), .out(subtractor_1_out));  // open: bin, bout
  Shifter #(.width(32)) shifter_1 (.in(Operand_1), .\dist (Operand_2[4:0]), .out(shifter_1_out));
  Multiplexer #(.width(32), .enable("false")) multiplexer_1 (
    .in0(adder_1_out), .in1(subtractor_1_out), .out(multiplexer_1_out), .sel(ALUOper[3]));
  Comparator #(.width(32)) comparator_1 (.a({32{1'b0}}), .b(subtractor_1_out), .eq(in_4));  // open: gt, lt
  Shifter #(.width(32)) shifter_2 (.in(Operand_1), .\dist (Operand_2[4:0]), .out(shifter_2_out));
  Shifter #(.width(32)) shifter_3 (.in(Operand_1), .\dist (Operand_2[4:0]), .out(shifter_3_out));
  Shifter #(.width(32), .shift("lr")) shifter_4 (.in(Operand_1), .\dist (Operand_2[4:0]), .out(shifter_4_out));
  Shifter #(.width(32), .shift("ar")) shifter_5 (.in(Operand_1), .\dist (Operand_2[4:0]), .out(shifter_5_out));
  assign xor_1_out = Operand_1 ^ Operand_2;  // XOR_Gate xor_1, 32 bits wide
  Multiplexer #(.width(32), .enable("false")) multiplexer_2 (
    .in0(shifter_4_out), .in1(shifter_5_out), .out(multiplexer_2_out), .sel(ALUOper[3]));
  assign or_1_out = Operand_1 | Operand_2;  // OR_Gate or_1, 32 bits wide
  assign and_1_out = Operand_1 & Operand_2;  // AND_Gate and_1, 32 bits wide
  Multiplexer #(.select(3), .width(32), .enable("false")) multiplexer_3 (
    .in0(multiplexer_1_out), .in1(shifter_1_out), .in2(shifter_2_out), .in3(shifter_3_out), .in4(xor_1_out),
    .in5(multiplexer_2_out), .in6(or_1_out), .in7(and_1_out), .out(ALUResultado), .sel(ALUOper[2:0]));

  // Other names for the same wires on the sheet: Input1[31:0] = Operand_1; Input2[31:0] = Operand_2;
  //   SftAmt[4:0] = in_3; Zero = in_4

  // Notes on the sheet:
  //   ADD
  //   SUB
  //   SLL
  //   SLT
  //   SLTU
  //   SRL
  //   SRA
endmodule

module ControlUnit (
  input  in_1,
  input  [31:0] in_2,
  output [1:0] out_3,
  output [3:0] out_4,
  output [2:0] out_5,
  output out_6,
  output [1:0] out_7,
  output out_8,
  output out_9,
  output out_10,
  output out_11,
  output out_12,
  output out_13
);


  // Other names for the same wires on the sheet: ALUSrcA = out_6; ALUSrcB[1:0] = out_7; Clock = in_1;
  //   Cycle[2:0] = out_5; Imm[1:0] = out_3; Instructions[31:0] = in_2; IorD = out_8; IRWrite = out_9;
  //   MemRead = out_10; MemToReg = out_13; MemWrite = out_11; OpCode[3:0] = out_4; RegWrite = out_12
endmodule

module PCControl (
  input  [2:0] in_1,
  input  in_2,
  input  [31:0] in_3,
  input  [2:0] in_4,
  input  [6:0] in_5,
  output PCSrc
);

  wire and_1_out, BEQ_out, BGE_out, BGEL_out, BLT_out, BLTU_out, BNE_out, comparator_1_eq, comparator_1_gt,
       comparator_1_lt, comparator_2_eq, comparator_2_gt, comparator_2_lt, comparator_3_eq, comparator_4_eq,
       decoder_1_out1, decoder_1_out2, demultiplexer_1_out0, demultiplexer_1_out1, demultiplexer_1_out4,
       demultiplexer_1_out5, demultiplexer_1_out6, demultiplexer_1_out7, IsBranch_out, multiplexer_1_out,
       not_1_out, or_1_out, or_2_out, or_3_out;

  Demultiplexer #(.select(3), .enable("false")) demultiplexer_1 (
    .out0(demultiplexer_1_out0), .out1(demultiplexer_1_out1), .out4(demultiplexer_1_out4),
    .out5(demultiplexer_1_out5), .out6(demultiplexer_1_out6), .out7(demultiplexer_1_out7), .in(1'b1),
    .sel(in_4));  // open: out2, out3
  Comparator #(.width(32)) comparator_1 (
    .a(in_3), .b({32{1'b0}}), .gt(comparator_1_gt), .eq(comparator_1_eq), .lt(comparator_1_lt));
  Comparator #(.width(32)) comparator_2 (
    .a(in_3), .b({32{1'b0}}), .gt(comparator_2_gt), .eq(comparator_2_eq), .lt(comparator_2_lt));
  not not_1 (not_1_out, comparator_1_eq);
  or or_1 (or_1_out, comparator_1_eq, comparator_1_gt);
  or or_2 (or_2_out, comparator_2_gt, comparator_2_eq);
  and BEQ (BEQ_out, comparator_1_eq, demultiplexer_1_out0);
  and BNE (BNE_out, demultiplexer_1_out1, not_1_out);
  and BLT (BLT_out, demultiplexer_1_out4, comparator_1_lt);
  and BGE (BGE_out, demultiplexer_1_out5, or_1_out);
  and BLTU (BLTU_out, demultiplexer_1_out6, comparator_2_lt);
  and BGEL (BGEL_out, demultiplexer_1_out7, or_2_out);
  Multiplexer #(.select(3), .enable("false")) multiplexer_1 (
    .in0(BEQ_out), .in1(BNE_out), .in4(BLT_out), .in5(BGE_out), .in6(BLTU_out), .in7(BGEL_out),
    .out(multiplexer_1_out), .sel(in_4));  // open: in2, in3
  Comparator #(.width(7)) comparator_3 (.a(in_5), .b(7'b1101111), .eq(comparator_3_eq));  // open: gt, lt
  Comparator #(.width(7)) comparator_4 (.a(in_5), .b(7'b1100011), .eq(comparator_4_eq));  // open: gt, lt
  Decoder #(.select(3), .enable("false")) decoder_1 (
    .out1(decoder_1_out1), .out2(decoder_1_out2), .sel(in_1));  // open: out0, out3, out4, out5, out6, out7
  and IsBranch (IsBranch_out, comparator_4_eq, decoder_1_out2, multiplexer_1_out);
  and and_1 (and_1_out, comparator_3_eq, decoder_1_out2);
  or or_3 (or_3_out, IsBranch_out, and_1_out);
  or or_4 (PCSrc, or_3_out, decoder_1_out1);

  // Other names for the same wires on the sheet: ALUResult[31:0] = in_3; Clock = in_2; Cycle[2:0] = in_1;
  //   Func3[2:0] = in_4; OpCode[6:0] = in_5
endmodule
