// Logisim project pipelined-with_hazards.circ as structural Verilog: 15 circuits, main circuit main
module main (
  input  Clock,
  output out_2
);

  wire alu_1_greater_than_zero, alu_1_less_than_zero, alu_1_zero, and_1_out, control_unit_1_memread,
       control_unit_1_memtoreg, control_unit_1_memwrite, control_unit_1_pcsrc, control_unit_1_regwrite,
       control_unit_1_signedop, ex_mem_1_mem_greaterthan, ex_mem_1_mem_greaterthan_2, ex_mem_1_mem_zero,
       ex_mem_1_memread_2, ex_mem_1_memtoreg_2, ex_mem_1_memwrite_2, ex_mem_1_regwrite_2,
       fowarding_unit_1_fw_01, fowarding_unit_1_fw_10, Hazard_Detection_if_id_write,
       Hazard_Detection_pcwrite, id_ex_1_memread_2, id_ex_1_memtoreg_2, id_ex_1_memwrite_2, id_ex_1_pcsrc_2,
       id_ex_1_regwrite_2, id_ex_1_signedop_2, mem_wb_1_memtoreg_2, mem_wb_1_regwrite_2, multiplexer_7_out,
       NE_out, not_1_out, or_1_out;
  wire [1:0] control_unit_1_alusrc, control_unit_1_branchcode, ex_mem_1_branchcode_2, id_ex_1_alusrc_2,
       id_ex_1_branchcode_2;
  wire [3:0] control_unit_1_aluop, id_ex_1_aluop_2;
  wire [4:0] ex_mem_1_mem_writeregister, id_ex_1_id_writeregister, mem_wb_1_writeregister_2;
  wire [31:0] adder_1_out, adder_2_out, alu_1_aluresultado, bit_extender_1_out, bit_extender_2_out,
       bit_extender_3_out, bit_extender_4_out, ex_mem_1_mem_aluresult, ex_mem_1_mem_pc_4,
       id_ex_1_id_imm_branch, id_ex_1_id_imm_jump, id_ex_1_id_imm_lw_xl, id_ex_1_id_imm_sw, id_ex_1_id_pc_4,
       id_ex_1_id_rs1, id_ex_1_id_rs2, if_id_1_id_instr, if_id_1_id_pc_4, Instruction_Memory_data,
       mem_wb_1_wb_aluresult, mem_wb_1_wb_readdata, memory_1_out_7, multiplexer_1_out, multiplexer_2_out,
       multiplexer_3_out, multiplexer_4_out, multiplexer_5_out, multiplexer_6_out, multiplexer_8_out, PC_q,
       registerfile_1_readdata1, registerfile_1_readdata2;

  buf or_1 (or_1_out, id_ex_1_signedop_2);  // OR_Gate
  Multiplexer #(.width(32), .enable("false")) multiplexer_1 (
    .in0(adder_1_out), .in1(multiplexer_2_out), .out(multiplexer_1_out), .sel(or_1_out));
  Register #(.width(32), .Select("low")) PC (
    .D(multiplexer_1_out), .en(Hazard_Detection_pcwrite), .Q(PC_q), .clk(Clock));  // open: clr
  Adder #(.width(32)) adder_1 (.a(32'h4), .b(PC_q), .out(adder_1_out));  // open: cin, cout
  IF_ID if_id_1 (
    .IF_PC_4(adder_1_out), .ID_PC_4(if_id_1_id_pc_4), .Clock(Clock), .IF_Instr(Instruction_Memory_data),
    .ID_Instr(if_id_1_id_instr), .IF_ID_Write(Hazard_Detection_if_id_write));
  ROM #(.dataWidth(32), .Select("low")) Instruction_Memory (.addr(PC_q[9:2]), .data(Instruction_Memory_data));
  Hazard_Detection Hazard_Detection (
    .ID_EX_rs2(id_ex_1_id_rs2[19:15]), .IF_ID_rs1(if_id_1_id_instr[24:20]),
    .IF_ID_rs2(if_id_1_id_instr[19:15]), .ID_EX_MemRead(id_ex_1_memread_2),
    .IF_ID_Write(Hazard_Detection_if_id_write), .PCWrite(Hazard_Detection_pcwrite), .Stall(out_2));
  Control_Unit control_unit_1 (
    .Instr(if_id_1_id_instr), .ALUOp(control_unit_1_aluop), .ALUSrc(control_unit_1_alusrc),
    .SignedOp(control_unit_1_signedop), .BranchCode(control_unit_1_branchcode), .PCSrc(control_unit_1_pcsrc),
    .MemRead(control_unit_1_memread), .MemWrite(control_unit_1_memwrite), .MemToReg(control_unit_1_memtoreg),
    .RegWrite(control_unit_1_regwrite));
  RegisterFile registerfile_1 (
    .Clock(Clock), .ReadRegister1(if_id_1_id_instr[24:20]), .ReadRegister2(if_id_1_id_instr[19:15]),
    .WriteRegister(mem_wb_1_writeregister_2), .WriteData(multiplexer_8_out),
    .ReadData1(registerfile_1_readdata1), .ReadData2(registerfile_1_readdata2));  // open: RegisterWrite
  ID_EX id_ex_1 (
    .Clock(Clock), .IF_PC_4(if_id_1_id_pc_4), .ID_PC_4(id_ex_1_id_pc_4), .IF_rs1(registerfile_1_readdata1),
    .ID_rs1(id_ex_1_id_rs1), .IF_rs2(registerfile_1_readdata2), .ID_rs2(id_ex_1_id_rs2),
    .IF_WriteRegister(if_id_1_id_instr[11:7]), .ID_WriteRegister(id_ex_1_id_writeregister),
    .IF_Imm_LW_xl(bit_extender_1_out), .ID_Imm_LW_xl(id_ex_1_id_imm_lw_xl), .IF_Imm_SW(bit_extender_2_out),
    .ID_Imm_SW(id_ex_1_id_imm_sw), .IF_Imm_Branch(bit_extender_3_out), .ID_Imm_Branch(id_ex_1_id_imm_branch),
    .IF_Imm_Jump(bit_extender_4_out), .ID_Imm_Jump(id_ex_1_id_imm_jump), .ALUOp(control_unit_1_aluop),
    .ALUOp_2(id_ex_1_aluop_2), .ALUSrc(control_unit_1_alusrc), .ALUSrc_2(id_ex_1_alusrc_2),
    .SignedOp(control_unit_1_signedop), .SignedOp_2(id_ex_1_signedop_2),
    .BranchCode(control_unit_1_branchcode), .BranchCode_2(id_ex_1_branchcode_2),
    .PCSrc(control_unit_1_pcsrc), .PCSrc_2(id_ex_1_pcsrc_2), .MemRead(control_unit_1_memread),
    .MemRead_2(id_ex_1_memread_2), .MemWrite(control_unit_1_memwrite), .MemWrite_2(id_ex_1_memwrite_2),
    .MemToReg(control_unit_1_memtoreg), .MemToReg_2(id_ex_1_memtoreg_2), .RegWrite(control_unit_1_regwrite),
    .RegWrite_2(id_ex_1_regwrite_2));
  assign bit_extender_1_out = {{20{if_id_1_id_instr[31]}}, if_id_1_id_instr[31:20]};  // Bit_Extender bit_extender_1
  assign bit_extender_2_out = {{20{if_id_1_id_instr[31]}}, {if_id_1_id_instr[31:25], if_id_1_id_instr[11:7]}};  // Bit_Extender bit_extender_2
  assign bit_extender_3_out = {{11{if_id_1_id_instr[31]}}, {if_id_1_id_instr[31], if_id_1_id_instr[19:12], if_id_1_id_instr[20], if_id_1_id_instr[30:21], 1'b0}};  // Bit_Extender bit_extender_3
  assign bit_extender_4_out = {{19{if_id_1_id_instr[31]}}, {if_id_1_id_instr[31], if_id_1_id_instr[7], if_id_1_id_instr[30:25], if_id_1_id_instr[11:8], 1'b0}};  // Bit_Extender bit_extender_4
  Multiplexer #(.width(32), .enable("false")) multiplexer_2 (
    .in0(ex_mem_1_mem_pc_4), .in1(adder_2_out), .out(multiplexer_2_out), .sel(and_1_out));
  and and_1 (and_1_out, multiplexer_7_out, not_1_out);
  Multiplexer #(.width(32), .enable("false")) multiplexer_3 (
    .in0(id_ex_1_id_imm_branch), .in1(id_ex_1_id_imm_jump), .out(multiplexer_3_out), .sel(id_ex_1_pcsrc_2));
  Multiplexer #(.width(32), .enable("false")) multiplexer_4 (
    .in0(id_ex_1_id_rs1), .in1(multiplexer_8_out), .out(multiplexer_4_out), .sel(fowarding_unit_1_fw_01));
  Multiplexer #(.width(32), .enable("false")) multiplexer_5 (
    .in0(multiplexer_6_out), .in1(multiplexer_8_out), .out(multiplexer_5_out), .sel(fowarding_unit_1_fw_10));
  Multiplexer #(.select(2), .width(32), .enable("false")) multiplexer_6 (
    .in0(id_ex_1_id_rs2), .in1(id_ex_1_id_imm_lw_xl), .in2(id_ex_1_id_imm_sw), .out(multiplexer_6_out),
    .sel(id_ex_1_alusrc_2));  // open: in3
  Fowarding_Unit fowarding_unit_1 (
    .ID_EX_RegisterRs(id_ex_1_id_rs1[24:20]), .ID_EX_RegisterRt(id_ex_1_id_rs2[19:15]),
    .EX_MEM_RegisterRd(ex_mem_1_mem_writeregister), .EX_MEM_RegWrite(ex_mem_1_regwrite_2),
    .MEM_WB_RegisterRd(mem_wb_1_writeregister_2), .MEM_WB_RegWrite(mem_wb_1_regwrite_2),
    .FW_01(fowarding_unit_1_fw_01), .FW_10(fowarding_unit_1_fw_10));
  not not_1 (not_1_out, id_ex_1_pcsrc_2);
  Adder #(.width(32)) adder_2 (.a(id_ex_1_id_pc_4), .b(multiplexer_3_out), .out(adder_2_out));  // open: cin, cout
  ALU alu_1 (
    .Operand_1(multiplexer_4_out), .Operand_2(multiplexer_5_out), .ALUOper(id_ex_1_aluop_2),
    .ALUResultado(alu_1_aluresultado), .Greater_than_zero(alu_1_greater_than_zero), .Zero(alu_1_zero),
    .Less_than_zero(alu_1_less_than_zero));  // open: in_4, Clock, in_3, SignedCmp
  EX_MEM ex_mem_1 (
    .Clock(Clock), .EX_PC_4(adder_2_out), .MEM_PC_4(ex_mem_1_mem_pc_4), .EX_ALUResult(alu_1_aluresultado),
    .MEM_ALUResult(ex_mem_1_mem_aluresult), .EX_WriteRegister(id_ex_1_id_writeregister),
    .MEM_WriteRegister(ex_mem_1_mem_writeregister), .EX_Zero(alu_1_zero), .MEM_Zero(ex_mem_1_mem_zero),
    .EX_GreaterThan(alu_1_greater_than_zero), .MEM_GreaterThan(ex_mem_1_mem_greaterthan),
    .EX_LessThan(alu_1_less_than_zero), .MEM_GreaterThan_2(ex_mem_1_mem_greaterthan_2),
    .BranchCode(id_ex_1_branchcode_2), .BranchCode_2(ex_mem_1_branchcode_2), .MemRead(id_ex_1_memread_2),
    .MemRead_2(ex_mem_1_memread_2), .MemWrite(id_ex_1_memwrite_2), .MemWrite_2(ex_mem_1_memwrite_2),
    .MemToReg(id_ex_1_memtoreg_2), .MemToReg_2(ex_mem_1_memtoreg_2), .RegWrite(id_ex_1_regwrite_2),
    .RegWrite_2(ex_mem_1_regwrite_2));
  or GE (ex_mem_1_regwrite_2, ex_mem_1_mem_zero, ex_mem_1_mem_greaterthan);
  or NE (NE_out, ex_mem_1_mem_greaterthan, ex_mem_1_mem_greaterthan_2);
  Multiplexer #(.select(2), .enable("false")) multiplexer_7 (
    .in0(ex_mem_1_mem_zero), .in1(NE_out), .in2(ex_mem_1_mem_greaterthan_2), .in3(ex_mem_1_regwrite_2),
    .out(multiplexer_7_out), .sel(ex_mem_1_branchcode_2));
  Memory memory_1 (
    .in_1(ex_mem_1_mem_aluresult), .out_7(memory_1_out_7), .in_3(ex_mem_1_memread_2),
    .in_4(ex_mem_1_memwrite_2), .in_5(Clock));  // open: in_2, in_6
  MEM_WB mem_wb_1 (
    .MEM_ALUResult(ex_mem_1_mem_aluresult), .WB_ALUResult(mem_wb_1_wb_aluresult), .Clock(Clock),
    .MEM_ReadData(memory_1_out_7), .WB_ReadData(mem_wb_1_wb_readdata), .RegWrite(ex_mem_1_regwrite_2),
    .RegWrite_2(mem_wb_1_regwrite_2), .MemToReg(ex_mem_1_memtoreg_2), .MemToReg_2(mem_wb_1_memtoreg_2),
    .WriteRegister(ex_mem_1_mem_writeregister), .WriteRegister_2(mem_wb_1_writeregister_2));
  Multiplexer #(.width(32), .enable("false")) multiplexer_8 (
    .in0(mem_wb_1_wb_aluresult), .in1(mem_wb_1_wb_readdata), .out(multiplexer_8_out),
    .sel(mem_wb_1_memtoreg_2));

  // Notes on the sheet:
  //   contents of Instruction_Memory (hex, n*v repeats v):
  //   1700093 2102023 a00093 a00113 a00193 a00213 a00293 a00313 108133 2281b3 610233 4202b3 6522223
  //   SW
  //   Jump
  //   Branch
endmodule

module Memory (
  input  [31:0] in_1,
  input  [31:0] in_2,
  input  in_3,
  input  in_4,
  input  in_5,
  input  in_6,
  output [31:0] out_7
);

  wire not_1_out;
  wire [31:0] multiplexer_1_out, ram_1_data, rom_1_data;

  not not_1 (not_1_out, in_6);
  ROM #(.dataWidth(32), .Select("low")) rom_1 (.addr(in_1[7:0]), .data(rom_1_data), .sel(in_6));
  Multiplexer #(.width(32), .enable("false")) multiplexer_1 (
    .in0(rom_1_data), .in1(ram_1_data), .out(multiplexer_1_out), .sel(in_6));
  RAM #(.dataWidth(32), .bus("separate"), .Select("low")) ram_1 (
    .addr(in_1[7:0]), .din(in_2), .data(ram_1_data), .str(in_4), .sel(not_1_out), .clk(in_5));  // open: ld, clr
  assign out_7 = in_3 ? multiplexer_1_out : 32'bz;  // Controlled_Buffer controlled_buffer_1

  // Other names for the same wires on the sheet: Clock = in_5; ReadAddress[7:0] = in_1[7:0];
  //   Instruction[31:0] = out_7; IorD = in_6; MemRead = in_3; MemWrite = in_4; WriteData[31:0] = in_2
endmodule

module InstructionRegister (
  input  [31:0] in_1,
  input  in_2,
  input  in_3,
  output [4:0] out_4,
  output [6:0] out_5,
  output [4:0] out_6,
  output [2:0] out_7,
  output [4:0] out_8,
  output [31:0] out_9
);

  Register #(.width(32), .Select("low")) register_1 (
    .D(in_1), .en(in_3), .Q({out_9[31:25], out_6, out_4, out_7, out_8, out_5}), .clk(in_2));  // open: clr

  assign out_9[24:0] = {out_6, out_4, out_7, out_8, out_5};

  // Other names for the same wires on the sheet: Clock = in_2; Instructions[31:0] = in_1; IRWrite = in_3;
  //   OpCode[6:0] = out_5; Output[31:0] = {out_9[31:25], out_6, out_4, out_7, out_8, out_5}; wr[4:0] = out_8;
  //   Func3[2:0] = out_7; rs1[4:0] = out_4; rs2[4:0] = out_6
endmodule

module MemoryDataRegister (
  input  [31:0] in_1,
  input  in_2,
  output [31:0] out_3
);

  Register #(.width(32), .Select("low")) Register (.D(in_1), .Q(out_3), .clk(in_2));  // open: en, clr

  // Other names for the same wires on the sheet: Clock = in_2; Instructions[31:0] = in_1; Output[31:0] = out_3
endmodule

module RegisterFile (
  input  Clock,
  input  [4:0] ReadRegister1,
  input  [4:0] ReadRegister2,
  input  [4:0] WriteRegister,
  input  [31:0] WriteData,
  input  RegisterWrite,
  output [31:0] ReadData1,
  output [31:0] ReadData2
);

  wire and_1_out, and_2_out, and_3_out, and_4_out, and_5_out, and_6_out, and_7_out, and_8_out, and_9_out,
       and_10_out, and_11_out, and_12_out, and_13_out, and_14_out, and_15_out, and_16_out, and_17_out,
       and_18_out, and_19_out, and_20_out, and_21_out, and_22_out, and_23_out, and_24_out, and_25_out,
       and_26_out, and_27_out, and_28_out, and_29_out, and_30_out, and_31_out, and_32_out, decoder_1_out0,
       decoder_1_out1, decoder_1_out2, decoder_1_out3, decoder_1_out4, decoder_1_out5, decoder_1_out6,
       decoder_1_out7, decoder_1_out8, decoder_1_out9, decoder_1_out10, decoder_1_out11, decoder_1_out12,
       decoder_1_out13, decoder_1_out14, decoder_1_out15, decoder_1_out16, decoder_1_out17, decoder_1_out18,
       decoder_1_out19, decoder_1_out20, decoder_1_out21, decoder_1_out22, decoder_1_out23, decoder_1_out24,
       decoder_1_out25, decoder_1_out26, decoder_1_out27, decoder_1_out28, decoder_1_out29, decoder_1_out30,
       decoder_1_out31;
  wire [31:0] register_1_q, register_2_q, register_3_q, register_4_q, register_5_q, register_6_q,
       register_7_q, register_8_q, register_9_q, register_10_q, register_11_q, register_12_q, register_13_q,
       register_14_q, register_15_q, register_16_q, register_17_q, register_18_q, register_19_q,
       register_20_q, register_21_q, register_22_q, register_23_q, register_24_q, register_25_q,
       register_26_q, register_27_q, register_28_q, register_29_q, register_30_q, register_31_q,
       register_32_q;

  Decoder #(.select(5), .enable("false")) decoder_1 (
    .out0(decoder_1_out0), .out1(decoder_1_out1), .out2(decoder_1_out2), .out3(decoder_1_out3),
    .out4(decoder_1_out4), .out5(decoder_1_out5), .out6(decoder_1_out6), .out7(decoder_1_out7),
    .out8(decoder_1_out8), .out9(decoder_1_out9), .out10(decoder_1_out10), .out11(decoder_1_out11),
    .out12(decoder_1_out12), .out13(decoder_1_out13), .out14(decoder_1_out14), .out15(decoder_1_out15),
    .out16(decoder_1_out16), .out17(decoder_1_out17), .out18(decoder_1_out18), .out19(decoder_1_out19),
    .out20(decoder_1_out20), .out21(decoder_1_out21), .out22(decoder_1_out22), .out23(decoder_1_out23),
    .out24(decoder_1_out24), .out25(decoder_1_out25), .out26(decoder_1_out26), .out27(decoder_1_out27),
    .out28(decoder_1_out28), .out29(decoder_1_out29), .out30(decoder_1_out30), .out31(decoder_1_out31),
    .sel(WriteRegister));
  and and_1 (and_1_out, decoder_1_out0, RegisterWrite);
  and and_2 (and_2_out, decoder_1_out8, RegisterWrite);
  and and_3 (and_3_out, decoder_1_out16, RegisterWrite);
  and and_4 (and_4_out, decoder_1_out24, RegisterWrite);
  and and_5 (and_5_out, decoder_1_out1, RegisterWrite);
  and and_6 (and_6_out, decoder_1_out9, RegisterWrite);
  and and_7 (and_7_out, decoder_1_out17, RegisterWrite);
  and and_8 (and_8_out, decoder_1_out25, RegisterWrite);
  and and_9 (and_9_out, decoder_1_out2, RegisterWrite);
  and and_10 (and_10_out, decoder_1_out10, RegisterWrite);
  and and_11 (and_11_out, decoder_1_out18, RegisterWrite);
  and and_12 (and_12_out, decoder_1_out26, RegisterWrite);
  and and_13 (and_13_out, decoder_1_out3, RegisterWrite);
  and and_14 (and_14_out, decoder_1_out11, RegisterWrite);
  and and_15 (and_15_out, decoder_1_out19, RegisterWrite);
  and and_16 (and_16_out, decoder_1_out27, RegisterWrite);
  and and_17 (and_17_out, decoder_1_out4, RegisterWrite);
  and and_18 (and_18_out, decoder_1_out12, RegisterWrite);
  and and_19 (and_19_out, decoder_1_out20, RegisterWrite);
  and and_20 (and_20_out, decoder_1_out28, RegisterWrite);
  and and_21 (and_21_out, decoder_1_out5, RegisterWrite);
  and and_22 (and_22_out, decoder_1_out13, RegisterWrite);
  and and_23 (and_23_out, decoder_1_out21, RegisterWrite);
  and and_24 (and_24_out, decoder_1_out29, RegisterWrite);
  and and_25 (and_25_out, decoder_1_out6, RegisterWrite);
  and and_26 (and_26_out, decoder_1_out7, RegisterWrite);
  and and_27 (and_27_out, decoder_1_out14, RegisterWrite);
  and and_28 (and_28_out, decoder_1_out15, RegisterWrite);
  and and_29 (and_29_out, decoder_1_out23, RegisterWrite);
  and and_30 (and_30_out, decoder_1_out22, RegisterWrite);
  and and_31 (and_31_out, decoder_1_out31, RegisterWrite);
  and and_32 (and_32_out, decoder_1_out30, RegisterWrite);
  Register #(.width(32), .Select("low")) register_1 (
    .D(WriteData), .en(and_26_out), .Q(register_1_q), .clk(Clock));  // open: clr
  Register #(.width(32), .Select("low")) register_2 (
    .D(WriteData), .en(and_28_out), .Q(register_2_q), .clk(Clock));  // open: clr
  Register #(.width(32), .Select("low")) register_3 (
    .D(WriteData), .en(and_29_out), .Q(register_3_q), .clk(Clock));  // open: clr
  Register #(.width(32), .Select("low")) register_4 (
    .D(WriteData), .en(and_31_out), .Q(register_4_q), .clk(Clock));  // open: clr
  Register #(.width(32), .Select("low")) register_5 (
    .D(WriteData), .en(and_25_out), .Q(register_5_q), .clk(Clock));  // open: clr
  Register #(.width(32), .Select("low")) register_6 (
    .D(WriteData), .en(and_27_out), .Q(register_6_q), .clk(Clock));  // open: clr
  Register #(.width(32), .Select("low")) register_7 (
    .D(WriteData), .en(and_30_out), .Q(register_7_q), .clk(Clock));  // open: clr
  Register #(.width(32), .Select("low")) register_8 (
    .D(WriteData), .en(and_32_out), .Q(register_8_q), .clk(Clock));  // open: clr
  Register #(.width(32), .Select("low")) register_9 (
    .D(WriteData), .en(and_21_out), .Q(register_9_q), .clk(Clock));  // open: clr
  Register #(.width(32), .Select("low")) register_10 (
    .D(WriteData), .en(and_22_out), .Q(register_10_q), .clk(Clock));  // open: clr
  Register #(.width(32), .Select("low")) register_11 (
    .D(WriteData), .en(and_23_out), .Q(register_11_q), .clk(Clock));  // open: clr
  Register #(.width(32), .Select("low")) register_12 (
    .D(WriteData), .en(and_24_out), .Q(register_12_q), .clk(Clock));  // open: clr
  Register #(.width(32), .Select("low")) register_13 (
    .D(WriteData), .en(and_17_out), .Q(register_13_q), .clk(Clock));  // open: clr
  Register #(.width(32), .Select("low")) register_14 (
    .D(WriteData), .en(and_18_out), .Q(register_14_q), .clk(Clock));  // open: clr
  Register #(.width(32), .Select("low")) register_15 (
    .D(WriteData), .en(and_19_out), .Q(register_15_q), .clk(Clock));  // open: clr
  Register #(.width(32), .Select("low")) register_16 (
    .D(WriteData), .en(and_20_out), .Q(register_16_q), .clk(Clock));  // open: clr
  Register #(.width(32), .Select("low")) register_17 (
    .D(WriteData), .en(and_13_out), .Q(register_17_q), .clk(Clock));  // open: clr
  Register #(.width(32), .Select("low")) register_18 (
    .D(WriteData), .en(and_14_out), .Q(register_18_q), .clk(Clock));  // open: clr
  Register #(.width(32), .Select("low")) register_19 (
    .D(WriteData), .en(and_15_out), .Q(register_19_q), .clk(Clock));  // open: clr
  Register #(.width(32), .Select("low")) register_20 (
    .D(WriteData), .en(and_16_out), .Q(register_20_q), .clk(Clock));  // open: clr
  Register #(.width(32), .Select("low")) register_21 (
    .D(WriteData), .en(and_9_out), .Q(register_21_q), .clk(Clock));  // open: clr
  Register #(.width(32), .Select("low")) register_22 (
    .D(WriteData), .en(and_10_out), .Q(register_22_q), .clk(Clock));  // open: clr
  Register #(.width(32), .Select("low")) register_23 (
    .D(WriteData), .en(and_11_out), .Q(register_23_q), .clk(Clock));  // open: clr
  Register #(.width(32), .Select("low")) register_24 (
    .D(WriteData), .en(and_12_out), .Q(register_24_q), .clk(Clock));  // open: clr
  Register #(.width(32), .Select("low")) register_25 (
    .D(WriteData), .en(and_5_out), .Q(register_25_q), .clk(Clock));  // open: clr
  Register #(.width(32), .Select("low")) register_26 (
    .D(WriteData), .en(and_6_out), .Q(register_26_q), .clk(Clock));  // open: clr
  Register #(.width(32), .Select("low")) register_27 (
    .D(WriteData), .en(and_7_out), .Q(register_27_q), .clk(Clock));  // open: clr
  Register #(.width(32), .Select("low")) register_28 (
    .D(WriteData), .en(and_8_out), .Q(register_28_q), .clk(Clock));  // open: clr
  Register #(.width(32), .Select("low")) register_29 (
    .D(WriteData), .en(and_1_out), .Q(register_29_q), .clk(Clock));  // open: clr
  Register #(.width(32), .Select("low")) register_30 (
    .D(WriteData), .en(and_2_out), .Q(register_30_q), .clk(Clock));  // open: clr
  Register #(.width(32), .Select("low")) register_31 (
    .D(WriteData), .en(and_3_out), .Q(register_31_q), .clk(Clock));  // open: clr
  Register #(.width(32), .Select("low")) register_32 (
    .D(WriteData), .en(and_4_out), .Q(register_32_q), .clk(Clock));  // open: clr
  Multiplexer #(.select(5), .width(32), .enable("false")) multiplexer_1 (
    .in0(register_1_q), .in1(register_5_q), .in2(register_9_q), .in3(register_13_q), .in4(register_17_q),
    .in5(register_21_q), .in6(register_25_q), .in7(register_29_q), .in8(register_2_q), .in9(register_6_q),
    .in10(register_10_q), .in11(register_14_q), .in12(register_18_q), .in13(register_22_q),
    .in14(register_26_q), .in15(register_30_q), .in16(register_3_q), .in17(register_7_q),
    .in18(register_11_q), .in19(register_15_q), .in20(register_19_q), .in21(register_23_q),
    .in22(register_27_q), .in23(register_31_q), .in24(register_4_q), .in25(register_8_q),
    .in26(register_12_q), .in27(register_16_q), .in28(register_20_q), .in29(register_24_q),
    .in30(register_28_q), .in31(register_32_q), .out(ReadData1), .sel(ReadRegister1));
  Multiplexer #(.select(5), .width(32), .enable("false")) multiplexer_2 (
    .in0(register_1_q), .in1(register_5_q), .in2(register_9_q), .in3(register_13_q), .in4(register_17_q),
    .in5(register_21_q), .in6(register_25_q), .in7(register_29_q), .in8(register_2_q), .in9(register_6_q),
    .in10(register_10_q), .in11(register_14_q), .in12(register_18_q), .in13(register_22_q),
    .in14(register_26_q), .in15(register_30_q), .in16(register_3_q), .in17(register_7_q),
    .in18(register_11_q), .in19(register_15_q), .in20(register_19_q), .in21(register_23_q),
    .in22(register_27_q), .in23(register_31_q), .in24(register_4_q), .in25(register_8_q),
    .in26(register_12_q), .in27(register_16_q), .in28(register_20_q), .in29(register_24_q),
    .in30(register_28_q), .in31(register_32_q), .out(ReadData2), .sel(ReadRegister2));

  // Notes on the sheet:
  //   Entradas
  //   Control
  //   Salidas
endmodule

module ALU (
  input  [31:0] Operand_1,
  input  [31:0] Operand_2,
  input  [4:0] in_3,
  input  in_4,
  input  [3:0] ALUOper,
  input  Clock,
  output [31:0] ALUResultado,
  output Greater_than_zero,
  output Zero,
  output Less_than_zero,
  output SignedCmp
);

  wire comparator_2_eq, comparator_2_gt, comparator_2_lt, comparator_3_eq, comparator_3_gt, comparator_3_lt;
  wire [31:0] adder_1_out, and_1_out, multiplexer_1_out, multiplexer_2_out, or_1_out, shifter_1_out,
       shifter_2_out, shifter_3_out, shifter_4_out, shifter_5_out, subtractor_1_out, xor_1_out;

  Adder #(.width(32)) adder_1 (.a(Operand_1), .b(Operand_2), .out(adder_1_out));  // open: cin, cout
  Subtractor #(.width(32)) subtractor_1 (.a(Operand_1), .b(Operand_2), .out(subtractor_1_out));  // open: bin, bout
  Shifter #(.width(32)) shifter_1 (.in(Operand_1), .\dist (Operand_2[4:0]), .out(shifter_1_out));
  Multiplexer #(.width(32), .enable("false")) multiplexer_1 (
    .in0(adder_1_out), .in1(subtractor_1_out), .out(multiplexer_1_out), .sel(ALUOper[3]));
  Comparator #(.width(32)) comparator_1 (.a({32{1'b0}}), .b(subtractor_1_out), .eq(in_4));  // open: gt, lt
  Shifter #(.width(32)) shifter_2 (.in(Operand_1), .\dist (Operand_2[4:0]), .out(shifter_2_out));
  Shifter #(.width(32)) shifter_3 (.in(Operand_1), .\dist (Operand_2[4:0]), .out(shifter_3_out));
  Shifter #(.width(32), .shift("lr")) shifter_4 (.in(Operand_1), .\dist (Operand_2[4:0]), .out(shifter_4_out));
  Shifter #(.width(32), .shift("ar")) shifter_5 (.in(Operand_1), .\dist (Operand_2[4:0]), .out(shifter_5_out));
  assign xor_1_out = Operand_1 ^ Operand_2;  // XOR_Gate xor_1, 32 bits wide
  Multiplexer #(.width(32), .enable("false")) multiplexer_2 (
    .in0(shifter_4_out), .in1(shifter_5_out), .out(multiplexer_2_out), .sel(ALUOper[3]));
  assign or_1_out = Operand_1 | Operand_2;  // OR_Gate or_1, 32 bits wide
  assign and_1_out = Operand_1 & Operand_2;  // AND_Gate and_1, 32 bits wide
  Comparator #(.width(32)) comparator_2 (
    .a(ALUResultado), .b({32{1'b0}}), .gt(comparator_2_gt), .eq(comparator_2_eq), .lt(comparator_2_lt));
  Comparator #(.width(32)) comparator_3 (
    .a(ALUResultado), .b({32{1'b0}}), .gt(comparator_3_gt), .eq(comparator_3_eq), .lt(comparator_3_lt));
  Multiplexer #(.enable("false")) multiplexer_3 (
    .in0(comparator_2_gt), .in1(comparator_3_gt), .out(Greater_than_zero), .sel(SignedCmp));
  Multiplexer #(.enable("false")) multiplexer_4 (
    .in0(comparator_2_eq), .in1(comparator_3_eq), .out(Zero), .sel(SignedCmp));
  Multiplexer #(.enable("false")) multiplexer_5 (
    .in0(comparator_2_lt), .in1(comparator_3_lt), .out(Less_than_zero), .sel(SignedCmp));
  Multiplexer #(.select(3), .width(32), .enable("false")) multiplexer_6 (
    .in0(multiplexer_1_out), .in1(shifter_1_out), .in2(shifter_2_out), .in3(shifter_3_out), .in4(xor_1_out),
    .in5(multiplexer_2_out), .in6(or_1_out), .in7(and_1_out), .out(ALUResultado), .sel(ALUOper[2:0]));

  // Other names for the same wires on the sheet: Input1[31:0] = Operand_1; Input2[31:0] = Operand_2;
  //   SftAmt[4:0] = in_3; Zero_t = in_4

  // Notes on the sheet:
  //   ADD
  //   SUB
  //   SLL
  //   SLT
  //   SLTU
  //   SRL
  //   SRA
endmodule

module ControlUnit (
  input  in_1,
  input  [31:0] in_2,
  output [1:0] out_3,
  output [3:0] out_4,
  output [2:0] out_5,
  output out_6,
  output [1:0] out_7,
  output out_8,
  output out_9,
  output out_10,
  output out_11,
  output out_12,
  output out_13
);


  // Other names for the same wires on the sheet: ALUSrcA = out_6; ALUSrcB[1:0] = out_7; Clock = in_1;
  //   Cycle[2:0] = out_5; Imm[1:0] = out_3; Instructions[31:0] = in_2; IorD = out_8; IRWrite = out_9;
  //   MemRead = out_10; MemToReg = out_13; MemWrite = out_11; OpCode[3:0] = out_4; RegWrite = out_12
endmodule

module PCControl (
  input  [2:0] in_1,
  input  in_2,
  input  [31:0] in_3,
  input  [2:0] in_4,
  input  [6:0] in_5,
  output PCSrc
);

  wire and_1_out, BEQ_out, BGE_out, BGEL_out, BLT_out, BLTU_out, BNE_out, comparator_1_eq, comparator_1_gt,
       comparator_1_lt, comparator_2_eq, comparator_2_gt, comparator_2_lt, comparator_3_eq, comparator_4_eq,
       decoder_1_out1, decoder_1_out2, demultiplexer_1_out0, demultiplexer_1_out1, demultiplexer_1_out4,
       demultiplexer_1_out5, demultiplexer_1_out6, demultiplexer_1_out7, IsBranch_out, multiplexer_1_out,
       not_1_out, or_1_out, or_2_out, or_3_out;

  Demultiplexer #(.select(3), .enable("false")) demultiplexer_1 (
    .out0(demultiplexer_1_out0), .out1(demultiplexer_1_out1), .out4(demultiplexer_1_out4),
    .out5(demultiplexer_1_out5), .out6(demultiplexer_1_out6), .out7(demultiplexer_1_out7), .in(1'b1),
    .sel(in_4));  // open: out2, out3
  Comparator #(.width(32)) comparator_1 (
    .a(in_3), .b({32{1'b0}}), .gt(comparator_1_gt), .eq(comparator_1_eq), .lt(comparator_1_lt));
  Comparator #(.width(32)) comparator_2 (
    .a(in_3), .b({32{1'b0}}), .gt(comparator_2_gt), .eq(comparator_2_eq), .lt(comparator_2_lt));
  not not_1 (not_1_out, comparator_1_eq);
  or or_1 (or_1_out, comparator_1_eq, comparator_1_gt);
  or or_2 (or_2_out, comparator_2_gt, comparator_2_eq);
  and BEQ (BEQ_out, comparator_1_eq, demultiplexer_1_out0);
  and BNE (BNE_out, demultiplexer_1_out1, not_1_out);
  and BLT (BLT_out, demultiplexer_1_out4, comparator_1_lt);
  and BGE (BGE_out, demultiplexer_1_out5, or_1_out);
  and BLTU (BLTU_out, demultiplexer_1_out6, comparator_2_lt);
  and BGEL (BGEL_out, demultiplexer_1_out7, or_2_out);
  Multiplexer #(.select(3), .enable("false")) multiplexer_1 (
    .in0(BEQ_out), .in1(BNE_out), .in4(BLT_out), .in5(BGE_out), .in6(BLTU_out), .in7(BGEL_out),
    .out(multiplexer_1_out), .sel(in_4));  // open: in2, in3
  Comparator #(.width(7)) comparator_3 (.a(in_5), .b(7'b1101111), .eq(comparator_3_eq));  // open: gt, lt
  Comparator #(.width(7)) comparator_4 (.a(in_5), .b(7'b1100011), .eq(comparator_4_eq));  // open: gt, lt
  Decoder #(.select(3), .enable("false")) decoder_1 (
    .out1(decoder_1_out1), .out2(decoder_1_out2), .sel(in_1));  // open: out0, out3, out4, out5, out6, out7
  and IsBranch (IsBranch_out, comparator_4_eq, decoder_1_out2, multiplexer_1_out);
  and and_1 (and_1_out, comparator_3_eq, decoder_1_out2);
  or or_3 (or_3_out, IsBranch_out, and_1_out);
  or or_4 (PCSrc, or_3_out, decoder_1_out1);

  // Other names for the same wires on the sheet: ALUResult[31:0] = in_3; Clock = in_2; Cycle[2:0] = in_1;
  //   Func3[2:0] = in_4; OpCode[6:0] = in_5
endmodule

module IF_ID (
  input  [31:0] IF_PC_4,
  input  Clock,
  input  [31:0] IF_Instr,
  input  IF_ID_Write,
  output [31:0] ID_PC_4,
  output [31:0] ID_Instr
);

  Register #(.width(32), .Select("low")) PC_4 (.D(IF_PC_4), .en(IF_ID_Write), .Q(ID_PC_4), .clk(Clock));  // open: clr
  Register #(.width(32), .Select("low")) Instr (
    .D(IF_Instr), .en(IF_ID_Write), .Q(ID_Instr), .clk(Clock));  // open: clr
endmodule

module ID_EX (
  input  Clock,
  input  [31:0] IF_PC_4,
  input  [31:0] IF_rs1,
  input  [31:0] IF_rs2,
  input  [4:0] IF_WriteRegister,
  input  [31:0] IF_Imm_LW_xl,
  input  [31:0] IF_Imm_SW,
  input  [31:0] IF_Imm_Branch,
  input  [31:0] IF_Imm_Jump,
  input  [3:0] ALUOp,
  input  [1:0] ALUSrc,
  input  SignedOp,
  input  [1:0] BranchCode,
  input  PCSrc,
  input  MemRead,
  input  MemWrite,
  input  MemToReg,
  input  RegWrite,
  output [31:0] ID_PC_4,
  output [31:0] ID_rs1,
  output [31:0] ID_rs2,
  output [4:0] ID_WriteRegister,
  output [31:0] ID_Imm_LW_xl,
  output [31:0] ID_Imm_SW,
  output [31:0] ID_Imm_Branch,
  output [31:0] ID_Imm_Jump,
  output [3:0] ALUOp_2,
  output [1:0] ALUSrc_2,
  output SignedOp_2,
  output [1:0] BranchCode_2,
  output PCSrc_2,
  output MemRead_2,
  output MemWrite_2,
  output MemToReg_2,
  output RegWrite_2
);

  Register #(.width(32), .Select("low")) ID_EX_PC_4 (.D(IF_PC_4), .Q(ID_PC_4), .clk(Clock));  // open: en, clr
  Register #(.width(32), .Select("low")) ID_EX_rs1 (.D(IF_rs1), .Q(ID_rs1), .clk(Clock));  // open: en, clr
  Register #(.width(32), .Select("low")) ID_EX_rs2 (.D(IF_rs2), .Q(ID_rs2), .clk(Clock));  // open: en, clr
  Register #(.width(5), .Select("low")) ID_EX_WriteRegister (
    .D(IF_WriteRegister), .Q(ID_WriteRegister), .clk(Clock));  // open: en, clr
  Register #(.width(32), .Select("low")) ID_EX_Imm_LW_xl (
    .D(IF_Imm_LW_xl), .Q(ID_Imm_LW_xl), .clk(Clock));  // open: en, clr
  Register #(.width(32), .Select("low")) ID_EX_Imm_SW (.D(IF_Imm_SW), .Q(ID_Imm_SW), .clk(Clock));  // open: en, clr
  Register #(.width(32), .Select("low")) ID_EX_Imm_Branch (
    .D(IF_Imm_Branch), .Q(ID_Imm_Branch), .clk(Clock));  // open: en, clr
  Register #(.width(32), .Select("low")) ID_EX_Imm_Jump (
    .D(IF_Imm_Jump), .Q(ID_Imm_Jump), .clk(Clock));  // open: en, clr
  Register #(.width(4), .Select("low")) register_1 (.D(ALUOp), .Q(ALUOp_2), .clk(Clock));  // open: en, clr
  Register #(.width(2), .Select("low")) register_2 (.D(ALUSrc), .Q(ALUSrc_2), .clk(Clock));  // open: en, clr
  Register #(.width(1), .Select("low")) register_3 (.D(SignedOp), .Q(SignedOp_2), .clk(Clock));  // open: en, clr
  Register #(.width(2), .Select("low")) register_4 (.D(BranchCode), .Q(BranchCode_2), .clk(Clock));  // open: en, clr
  Register #(.width(1), .Select("low")) register_5 (.D(PCSrc), .Q(PCSrc_2), .clk(Clock));  // open: en, clr
  Register #(.width(1), .Select("low")) register_6 (.D(MemRead), .Q(MemRead_2), .clk(Clock));  // open: en, clr
  Register #(.width(1), .Select("low")) register_7 (.D(MemWrite), .Q(MemWrite_2), .clk(Clock));  // open: en, clr
  Register #(.width(1), .Select("low")) register_8 (.D(MemToReg), .Q(MemToReg_2), .clk(Clock));  // open: en, clr
  Register #(.width(1), .Select("low")) register_9 (.D(RegWrite), .Q(RegWrite_2), .clk(Clock));  // open: en, clr
endmodule

module EX_MEM (
  input  Clock,
  input  [31:0] EX_PC_4,
  input  [31:0] EX_ALUResult,
  input  [4:0] EX_WriteRegister,
  input  EX_Zero,
  input  EX_GreaterThan,
  input  EX_LessThan,
  input  [1:0] BranchCode,
  input  MemRead,
  input  MemWrite,
  input  MemToReg,
  input  RegWrite,
  output [31:0] MEM_PC_4,
  output [31:0] MEM_ALUResult,
  output [4:0] MEM_WriteRegister,
  output MEM_Zero,
  output MEM_GreaterThan,
  output MEM_GreaterThan_2,
  output [1:0] BranchCode_2,
  output MemRead_2,
  output MemWrite_2,
  output MemToReg_2,
  output RegWrite_2
);

  Register #(.width(32), .Select("low")) EX_MEM_PC_4 (.D(EX_PC_4), .Q(MEM_PC_4), .clk(Clock));  // open: en, clr
  Register #(.width(32), .Select("low")) EX_MEM_ALUResult (
    .D(EX_ALUResult), .Q(MEM_ALUResult), .clk(Clock));  // open: en, clr
  Register #(.width(5), .Select("low")) EX_MEM_WriteRegister (
    .D(EX_WriteRegister), .Q(MEM_WriteRegister), .clk(Clock));  // open: en, clr
  Register #(.width(1), .Select("low")) EX_MEM_Zero (.D(EX_Zero), .Q(MEM_Zero), .clk(Clock));  // open: en, clr
  Register #(.width(1), .Select("low")) EX_MEM_GreaterThan (
    .D(EX_GreaterThan), .Q(MEM_GreaterThan), .clk(Clock));  // open: en, clr
  Register #(.width(1), .Select("low")) EX_MEM_GreaterThan_2 (
    .D(EX_LessThan), .Q(MEM_GreaterThan_2), .clk(Clock));  // open: en, clr
  Register #(.width(2), .Select("low")) register_1 (.D(BranchCode), .Q(BranchCode_2), .clk(Clock));  // open: en, clr
  Register #(.width(1), .Select("low")) register_2 (.D(MemRead), .Q(MemRead_2), .clk(Clock));  // open: en, clr
  Register #(.width(1), .Select("low")) register_3 (.D(MemWrite), .Q(MemWrite_2), .clk(Clock));  // open: en, clr
  Register #(.width(1), .Select("low")) register_4 (.D(MemToReg), .Q(MemToReg_2), .clk(Clock));  // open: en, clr
  Register #(.width(1), .Select("low")) register_5 (.D(RegWrite), .Q(RegWrite_2), .clk(Clock));  // open: en, clr
endmodule

module MEM_WB (
  input  [31:0] MEM_ALUResult,
  input  Clock,
  input  [31:0] MEM_ReadData,
  input  RegWrite,
  input  MemToReg,
  input  [4:0] WriteRegister,
  output [31:0] WB_ALUResult,
  output [31:0] WB_ReadData,
  output RegWrite_2,
  output MemToReg_2,
  output [4:0] WriteRegister_2
);

  Register #(.width(32), .Select("low")) MEM_WB_ALUResult (
    .D(MEM_ALUResult), .Q(WB_ALUResult), .clk(Clock));  // open: en, clr
  Register #(.width(32), .Select("low")) MEM_WB_ReadData (
    .D(MEM_ReadData), .Q(WB_ReadData), .clk(Clock));  // open: en, clr
  Register #(.width(1), .Select("low")) register_1 (.D(RegWrite), .Q(RegWrite_2), .clk(Clock));  // open: en, clr
  Register #(.width(1), .Select("low")) register_2 (.D(MemToReg), .Q(MemToReg_2), .clk(Clock));  // open: en, clr
  Register #(.width(5), .Select("low")) register_3 (
    .D(WriteRegister), .Q(WriteRegister_2), .clk(Clock));  // open: en, clr
endmodule

module Control_Unit (
  input  [31:0] Instr,
  output [3:0] ALUOp,
  output [1:0] ALUSrc,
  output SignedOp,
  output [1:0] BranchCode,
  output PCSrc,
  output MemRead,
  output MemWrite,
  output MemToReg,
  output RegWrite
);

  wire Branch, Jump, LB, LH, SB, SH, Type_I, Type_R;

  and and_1 (Type_R, Instr[0], Instr[1], ~Instr[2], ~Instr[3], Instr[4], Instr[5], ~Instr[6]);  // AND_Gate
  and and_2 (Type_I, Instr[0], Instr[1], ~Instr[2], ~Instr[3], Instr[4], ~Instr[5], ~Instr[6]);  // AND_Gate
  and and_3 (MemRead, Instr[0], Instr[1], ~Instr[2], ~Instr[3], ~Instr[4], ~Instr[5], ~Instr[6]);  // AND_Gate
  and and_4 (ALUSrc[1], Instr[0], Instr[1], ~Instr[2], ~Instr[3], ~Instr[4], Instr[5], ~Instr[6]);  // AND_Gate
  and and_5 (Branch, Instr[0], Instr[1], ~Instr[2], ~Instr[3], ~Instr[4], Instr[5], Instr[6]);  // AND_Gate
  and and_6 (Jump, Instr[0], Instr[1], Instr[2], Instr[3], ~Instr[4], Instr[5], Instr[6]);  // AND_Gate
  and and_7 (LB, ~Instr[0], ~Instr[1], ~Instr[2], Instr[3], ~Instr[4], ~Instr[5], Instr[6]);  // AND_Gate
  and and_8 (LH, Instr[0], ~Instr[1], ~Instr[2], Instr[3], ~Instr[4], ~Instr[5], Instr[6]);  // AND_Gate
  and and_9 (SB, ~Instr[0], ~Instr[1], ~Instr[2], Instr[3], Instr[4], ~Instr[5], Instr[6]);  // AND_Gate
  and and_10 (SH, Instr[0], ~Instr[1], ~Instr[2], Instr[3], ~Instr[4], ~Instr[5], Instr[6]);  // AND_Gate
  or or_1 (ALUSrc[0], MemRead, Type_I);
  or or_2 (PCSrc, Branch, Jump);
  or or_3 (MemToReg, MemRead, ALUSrc[1]);
  or or_4 (RegWrite, Type_R, Type_I, MemRead, ALUSrc[1]);

  assign ALUOp = {Instr[14:12], Instr[30]};
  assign BranchCode = {Instr[14], Instr[12]};
  assign MemWrite = ALUSrc[1];
  assign SignedOp = Instr[13];

  // Other names for the same wires on the sheet: func7b1 = Instr[30]; funct7[6:0] = Instr[31:25];
  //   funct3[2:0] = Instr[14:12]; Store = ALUSrc[1]; OpCode[6:0] = Instr[6:0]; Load = MemRead
endmodule

module Fowarding_Unit (
  input  [4:0] ID_EX_RegisterRs,
  input  [4:0] ID_EX_RegisterRt,
  input  [4:0] EX_MEM_RegisterRd,
  input  EX_MEM_RegWrite,
  input  [4:0] MEM_WB_RegisterRd,
  input  MEM_WB_RegWrite,
  output FW_01,
  output FW_10
);

  wire and_1_out, and_2_out, and_3_out, and_4_out, and_5_out, and_6_out, comparator_1_eq, comparator_2_eq,
       comparator_3_eq, comparator_4_eq, comparator_5_eq, comparator_6_eq, not_1_out, not_2_out;

  Comparator #(.width(5)) comparator_1 (.a(EX_MEM_RegisterRd), .b({5{1'b0}}), .eq(comparator_1_eq));  // open: gt, lt
  Comparator #(.width(5)) comparator_2 (.a(MEM_WB_RegisterRd), .b({5{1'b0}}), .eq(comparator_2_eq));  // open: gt, lt
  not not_1 (not_1_out, comparator_1_eq);
  and and_1 (and_1_out, not_1_out, EX_MEM_RegWrite);
  not not_2 (not_2_out, comparator_2_eq);
  and and_2 (and_2_out, not_2_out, MEM_WB_RegWrite);
  Comparator #(.width(5)) comparator_3 (
    .a(ID_EX_RegisterRs), .b(EX_MEM_RegisterRd), .eq(comparator_3_eq));  // open: gt, lt
  Comparator #(.width(5)) comparator_4 (
    .a(ID_EX_RegisterRt), .b(EX_MEM_RegisterRd), .eq(comparator_4_eq));  // open: gt, lt
  Comparator #(.width(5)) comparator_5 (
    .a(MEM_WB_RegisterRd), .b(ID_EX_RegisterRs), .eq(comparator_5_eq));  // open: gt, lt
  Comparator #(.width(5)) comparator_6 (
    .a(MEM_WB_RegisterRd), .b(ID_EX_RegisterRt), .eq(comparator_6_eq));  // open: gt, lt
  and and_3 (and_3_out, comparator_3_eq, and_1_out);
  or or_1 (FW_01, and_3_out, and_4_out);
  and and_4 (and_4_out, comparator_4_eq, and_1_out);
  and and_5 (and_5_out, and_2_out, comparator_5_eq);
  or or_2 (FW_10, and_5_out, and_6_out);
  and and_6 (and_6_out, and_2_out, comparator_6_eq);
endmodule

module Hazard_Detection (
  input  [4:0] ID_EX_rs2,
  input  [4:0] IF_ID_rs1,
  input  [4:0] IF_ID_rs2,
  input  ID_EX_MemRead,
  output IF_ID_Write,
  output PCWrite,
  output Stall
);

  wire comparator_1_eq, comparator_2_eq, or_1_out;

  Comparator #(.width(5)) comparator_1 (.a(ID_EX_rs2), .b(IF_ID_rs1), .eq(comparator_1_eq));  // open: gt, lt
  Comparator #(.width(5)) comparator_2 (.a(ID_EX_rs2), .b(IF_ID_rs2), .eq(comparator_2_eq));  // open: gt, lt
  not not_1 (IF_ID_Write, Stall);
  or or_1 (or_1_out, comparator_1_eq, comparator_2_eq);
  and and_1 (Stall, ID_EX_MemRead, or_1_out);

  assign PCWrite = IF_ID_Write;

  // Notes on the sheet:
  //   Entradas
  //   Salidas
endmodule
