// Logisim project B97670-A.circ as structural Verilog: 1 circuit, main circuit main
module main (
  input  [31:0] DataIn,
  input  [31:0] Address,
  input  MemRead,
  input  MemWrite,
  output [31:0] DataOut
);

  wire Clock;
  wire [7:0] multiplexer_1_out, ram_2_data, ram_3_data, ram_4_data, ram_5_data;
  wire [31:0] ram_1_data;

  Clock u_Clock (.out(Clock));
  RAM #(.dataWidth(32), .bus("separate")) ram_1 (
    .addr(Address[7:0]), .din(DataIn), .data(ram_1_data), .str(MemWrite), .clk(Clock), .ld(MemRead));  // open: sel, clr
  RAM #(.bus("separate")) ram_2 (
    .addr(Address[7:0]), .din(ram_1_data[7:0]), .data(ram_2_data), .str(MemWrite), .clk(Clock), .ld(MemRead));  // open: sel, clr
  RAM #(.bus("separate")) ram_3 (
    .addr(Address[7:0]), .din(ram_1_data[15:8]), .data(ram_3_data), .str(MemWrite), .clk(Clock), .ld(MemRead));  // open: sel, clr
  RAM #(.bus("separate")) ram_4 (
    .addr(Address[7:0]), .din(ram_1_data[23:16]), .data(ram_4_data), .str(MemWrite), .clk(Clock), .ld(MemRead));  // open: sel, clr
  RAM #(.bus("separate")) ram_5 (
    .addr(Address[7:0]), .din(ram_1_data[31:24]), .data(ram_5_data), .str(MemWrite), .clk(Clock), .ld(MemRead));  // open: sel, clr
  Multiplexer #(.select(2), .width(8)) multiplexer_1 (
    .in0(ram_2_data), .in1(ram_3_data), .in2(ram_4_data), .in3(ram_5_data), .out(multiplexer_1_out),
    .en(Clock));  // open: sel
  assign DataOut = {{24{1'b0}}, multiplexer_1_out};  // Bit_Extender bit_extender_1
endmodule
